// Logisim project Final Project Pipeline.circ as structural Verilog: 41 circuits, main circuit main
module main (
  input  in_1,
  input  in_2,
  input  in_3,
  input  clear,
  input  clear_2,
  input  clear_3,
  input  clear_4
);

  wire ALUSrc, ALUSrc_1, beq, beqz, bgez, blez, bltz, bne, bnez, bqtz, Branch, BranchTaken, CLK, EX,
       hazard_detection_unit_1_stall, hazard_detection_unit_1_stall_2, Imm, Imm_1, Imm_2, Imm_3, J, J_1, J_2,
       J_3, JR, JR2, JR3, JR_1, MemRd, MemRd_1, MemRd_2, MemRd_3, MemToReg, MemToReg_1, MemToReg_2,
       MemToReg_3, MemWr, MemWr_1, MemWr_2, not_1_out, not_2_out, or_1_out, R7, R7_1, R7_2, R7_3, reg1, reg2,
       reg3, reg3_1, RegWr, RegWr_1, RegWr_2, RegWr_3, SET, SET_1, SET_2, SET_3, SSET, SSET_1, SSET_2,
       SSET_3, stall;
  wire [1:0] func, func_1;
  wire [2:0] Fwd_c, Fwd_d, id_ex_1_rd_2, id_ex_1_reg7_2, Rd_1, Rd_2, Rd_3, Rs, Rs_IF_ID, Rt, Rt_IF_ID;
  wire [3:0] FwdA, FwdB, pc_next, pc_next_1, pc_next_2, pc_next_3, pc_next_t;
  wire [4:0] ALUop, ALUop_1, Imm5_1, Imm5_2, Imm5_3, opcode, opcode1, opcode2, opcode3;
  wire [4:2] Imm5;
  wire [7:0] Imm8_1, Imm8_2, mem_wb_1_imm8_2;
  wire [7:5] Imm8;
  wire [10:0] Imm11_1, Imm11_2, Imm11_3;
  wire [10:8] Imm11;
  wire [15:0] multiplexer_1_out, rom_1_data;
  wire [18:0] multiplexer_8_out;
  wire [19:0] bit_extender_5_out, NPC, PC, PC_IF_ID;
  wire [31:0] A, adder_1_out, alu_1_result, ALU_result_2, ALU_result_3, B, bit_extender_1_out,
       bit_extender_2_out, bit_extender_3_out, bit_extender_4_out, BusA, BusA_1, BusB, BusB_1,
       data_out_of_memory_3, ex_mem_1_busb_2, id_ex_1_imm_singex, jal_jalr__v___1, jal_jalr__v___3,
       jal_jalr__v_____2, multiplexer_3_out, multiplexer_5_out, multiplexer_12_out, multiplexer_13_out,
       multiplexer_14_out, multiplexer_15_out, ram_1_data, register_file_1_bus_a, register_file_1_bus_b,
       SET___value_2, SET__v___3, SSET__v___3, SSET_value_2, WB_data;

  Counter #(.width(20), .max('hfffff)) u_PC (
    .load(not_1_out), .D(NPC), .count(in_1), .Q(PC), .clk(CLK), .clr(in_1));  // open: carry
  not not_1 (not_1_out, stall);
  Clock clock_1 (.out(CLK));
  ROM #(.addrWidth(20), .dataWidth(16)) rom_1 (.addr(PC), .data(rom_1_data), .sel(1'b1));
  PC pc_2 (
    .Pc(PC), .Offset2_imm8({Imm8, Imm5, func}), .Jumb_imm11({Imm11, Imm8, Imm5, func}), .Branch(Branch),
    .Reg_Rd(BusB), .offset_1_imm5({Imm5, func}), .Imm(Imm_3), .J(J), .JR(JR), .beq(beq), .bneq(bne),
    .beqz(beqz), .bnez(bnez), .bltz(bltz), .bgez(bgez), .bgtz(bqtz), .blez(blez), .NPC(NPC),
    .PC_Next(pc_next_t), .Pc_IF_ID(PC_IF_ID));
  or or_1 (or_1_out, J, BranchTaken, JR);
  not not_2 (not_2_out, stall);
  IF_ID_register if_id_register_1 (
    .PC(PC), .Inst(multiplexer_1_out), .PC_2(PC_IF_ID), .Inst_2({opcode, Imm11, Imm8, Imm5, func}),
    .clk(CLK), .Enable(not_2_out), .clear(in_2));
  Multiplexer #(.width(16), .enable("false")) multiplexer_1 (
    .in0(rom_1_data), .in1(16'h1000), .out(multiplexer_1_out), .sel(or_1_out));
  assign bit_extender_1_out = {{12{PC_IF_ID[19]}}, PC_IF_ID};  // Bit_Extender bit_extender_1
  Hazard_detection_unit hazard_detection_unit_1 (
    .stall(hazard_detection_unit_1_stall), .IF_ID_Rs(Rs_IF_ID), .ID_EX_MemRd(MemRd_1), .IF_ID_SSET(SSET),
    .IF_ID_Rt(Rt_IF_ID), .ID_Ex_Rd(Rd_1), .IF_ID_Rd(Imm11), .Ex_Mem_Rd(Rd_2), .branch_taken(BranchTaken),
    .JR_jalr(JR), .Ex_Mem_MemRD(MemRd_2), .Ex_Mem_RegWr(RegWr_2), .Ex_Mem_SSET(SSET_2),
    .ID_EX_RegWr(RegWr_1), .ID_EX_SSET(SSET_1), .opcode_if_id(opcode), .next_pc(pc_next_t),
    .stall_2(hazard_detection_unit_1_stall_2));
  assign bit_extender_2_out = {{27{Imm5[4]}}, {Imm5, func}};  // Bit_Extender bit_extender_2
  assign bit_extender_3_out = {{24{Imm8[7]}}, {Imm8, Imm5, func}};  // Bit_Extender bit_extender_3
  or or_2 (stall, hazard_detection_unit_1_stall, hazard_detection_unit_1_stall_2);
  assign bit_extender_4_out = {{27{1'b0}}, {Imm5, func}};  // Bit_Extender bit_extender_4
  Multiplexer #(.width(3), .enable("false")) multiplexer_2 (.in0(Imm8), .in1(Imm11), .out(Rs_IF_ID), .sel(reg1));
  Multiplexer #(.width(32), .enable("false")) multiplexer_3 (
    .in0(bit_extender_4_out), .in1(bit_extender_2_out), .out(multiplexer_3_out), .sel(EX));
  Adder #(.width(32)) adder_1 (.a(bit_extender_1_out), .b(32'h1), .out(adder_1_out));  // open: cin, cout
  comparator comparator_1 (
    .Bne(bne), .Beq(beq), .BNEZ(bnez), .BEQZ(beqz), .BGTZ(bqtz), .BLTZ(bltz), .BGEZ(bgez), .BLEZ(blez),
    .in_1(BusA), .in_2(BusB));
  control_unit control_unit_1 (
    .Reg1(reg1), .Reg2(reg2), .Reg3(reg3), .Ex(EX), .Imm(Imm), .SET(SET), .SSET(SSET), .RegWr(RegWr),
    .ALUSrc(ALUSrc), .ALUop(ALUop), .MemToReg(MemToReg), .MemRd(MemRd), .MemWr(MemWr), .Branch(Branch),
    .J(J), .JR(JR), .R7(R7), .Opcode(opcode), .PC_NEXT(pc_next_t));
  Multiplexer #(.width(3), .enable("false")) multiplexer_4 (.in0(Imm5), .in1(Imm11), .out(Rt_IF_ID), .sel(reg2));
  Multiplexer #(.width(32), .enable("false")) multiplexer_5 (
    .in0(multiplexer_3_out), .in1(bit_extender_3_out), .out(multiplexer_5_out), .sel(Imm));
  register__file register_file_1 (
    .bus_w(WB_data), .bus_A(register_file_1_bus_a), .bus_B(register_file_1_bus_b), .RegWr(RegWr_3),
    .Rd(Rd_3), .CLK(CLK), .clear(clear), .Rs(Rs_IF_ID), .Rt(Rt_IF_ID));
  branch_taken branch_taken_1 (
    .Branch(Branch), .Bne(bne), .Beq(beq), .BNEZ(bnez), .Branch_Taken(BranchTaken), .BEQZ(beqz), .BGTZ(bqtz),
    .BLTZ(bltz), .BGEZ(bgez), .BLEZ(blez), .PC_Next(pc_next_t));
  Multiplexer #(.select(3), .width(32), .enable("false")) multiplexer_6 (
    .in0(register_file_1_bus_a), .in1(ALU_result_2), .in2(SSET_value_2), .in3(SET___value_2),
    .in4(jal_jalr__v_____2), .in5(register_file_1_bus_a), .in6(register_file_1_bus_a),
    .in7(register_file_1_bus_a), .out(BusA), .sel(Fwd_c));
  Multiplexer #(.select(3), .width(32), .enable("false")) multiplexer_7 (
    .in0(register_file_1_bus_b), .in1(ALU_result_2), .in2(SSET_value_2), .in3(SET___value_2),
    .in4(jal_jalr__v_____2), .in5(register_file_1_bus_b), .in6(register_file_1_bus_b),
    .in7(register_file_1_bus_b), .out(BusB), .sel(Fwd_d));
  Branch_Fwd_unit branch_fwd_unit_1 (
    .Ex_Mem_SSET(SSET_2), .Ex_Mem_set(SET_2), .Ex_Mem____j(J_2), .Ex_Mem____jr(JR2), .JR(JR),
    .branch(Branch), .opcode_ex_mem(opcode2), .Ex_Mem_RegWr(RegWr_2), .ex_mem_mem_read(MemRd_2),
    .Ex_Mem_Rd(Rd_2), .next_pc(pc_next_t), .FWD_C(Fwd_c), .FWD_D(Fwd_d), .IF_ID_Rs(Rs_IF_ID), .IF_ID_Rd(Imm11));
  Multiplexer #(.width(19), .enable("false")) multiplexer_8 (
    .in0({pc_next, ALUop, ALUSrc, reg3, MemWr, MemRd, RegWr, MemToReg, R7, SSET, SET, Imm}),
    .in1({19{1'b0}}), .out(multiplexer_8_out), .sel(stall));
  ID_EX id_ex_1 (
    .Imm8({Imm8, Imm5, func}), .PC_1(adder_1_out), .Imm_SignEX(multiplexer_5_out), .Rd(Imm11), .Rs(Rs_IF_ID),
    .Rt(Rt_IF_ID), .Imm8_2(Imm8_1), .PC_1_2(jal_jalr__v___1), .Imm_SingEx(id_ex_1_imm_singex),
    .Reg7_2(id_ex_1_reg7_2), .Rd_2(id_ex_1_rd_2), .Rs_2(Rs), .Rt_2(Rt), .SET(multiplexer_8_out[1]),
    .SSET(multiplexer_8_out[2]), .MemToReg(multiplexer_8_out[4]), .RegWr(multiplexer_8_out[5]),
    .MemRd(multiplexer_8_out[6]), .MemWr(multiplexer_8_out[7]), .Reg3(multiplexer_8_out[8]),
    .ALUSrc(multiplexer_8_out[9]), .ALUop(multiplexer_8_out[14:10]), .R7(multiplexer_8_out[3]),
    .ALUop_2(ALUop_1), .ALUSrc_2(ALUSrc_1), .Reg3_2(reg3_1), .MemWr_2(MemWr_1), .MemRd_2(MemRd_1),
    .RegWr_2(RegWr_1), .MemToReg_2(MemToReg_1), .SET_2(SET_1), .SSET_2(SSET_1), .R7_2(R7_1), .Reg7(3'b111),
    .BusA(BusA), .BusA_2(BusA_1), .BusB(BusB), .BusB_2(BusB_1), .CLK(CLK), .Func(func), .Func_2(func_1),
    .pc_next_2(pc_next_1), .pc_next(multiplexer_8_out[18:15]), .Imm5({Imm5, func}), .Imm5_2(Imm5_1),
    .Imm11({Imm11, Imm8, Imm5, func}), .Imm11_2(Imm11_1), .Imm(multiplexer_8_out[0]), .Imm_2(Imm_1),
    .clear(clear_4), .opcode(opcode), .opcode_2(opcode1), .J(J), .J_2(J_1), .JR(JR), .JR_2(JR_1));
  Multiplexer #(.width(3), .enable("false")) multiplexer_9 (
    .in0(id_ex_1_rd_2), .in1(id_ex_1_reg7_2), .out(Rd_1), .sel(reg3_1));
  Multiplexer #(.select(4), .width(32), .enable("false")) multiplexer_10 (
    .in0(BusA_1), .in1(ALU_result_2), .in2(SSET_value_2), .in3(SET___value_2), .in4(jal_jalr__v_____2),
    .in5(ALU_result_3), .in6(data_out_of_memory_3), .in7(SSET__v___3), .in8(SET__v___3),
    .in9(jal_jalr__v___3), .in10(BusA_1), .in11(BusA_1), .in12(BusA_1), .in13(BusA_1), .in14(BusA_1),
    .in15(BusA_1), .out(A), .sel(FwdA));
  Multiplexer #(.select(4), .width(32), .enable("false")) multiplexer_11 (
    .in0(BusB_1), .in1(ALU_result_2), .in2(SSET_value_2), .in3(SET___value_2), .in4(jal_jalr__v_____2),
    .in5(ALU_result_3), .in6(data_out_of_memory_3), .in7(SSET__v___3), .in8(SET__v___3),
    .in9(jal_jalr__v___3), .in10(BusB_1), .in11(BusB_1), .in12(BusB_1), .in13(BusB_1), .in14(BusB_1),
    .in15(BusB_1), .out(B), .sel(FwdB));
  Multiplexer #(.width(32), .enable("false")) multiplexer_12 (
    .in0(B), .in1(id_ex_1_imm_singex), .out(multiplexer_12_out), .sel(ALUSrc_1));
  ALU alu_1 (.func(func_1), .in_3(A), .in_4(multiplexer_12_out), .result(alu_1_result), .ALUop(ALUop_1));
  Forward_Unit forward_unit_1 (
    .ID_EX_Rs(Rs), .EX_Mem_Rd(Rd_2), .ID_EX_Rt(Rt), .Mem_WB_Rd(Rd_3), .ID_EX_Rd(Rd_1), .ID_Ex_SSET(SSET_1),
    .Ex_Mem_RegWr(RegWr_2), .Mem_WB_RegWr(RegWr_3), .opcode_id_ex(opcode1), .Ex_Mem_sset(SSET_2),
    .Ex_Mem_set(SET_2), .Ex_Mem_j(J_2), .Ex_Mem_jr(JR2), .Mem_WB_sset(SSET_3), .Mem_WB_set(SET_3),
    .Mem_WB_j(J_3), .Mem_WB_mem_read(MemRd_3), .opcode_ex_mem(opcode2), .opcode_mem_wb(opcode3),
    .ex_mem_mem_read(MemRd_2), .Mem_WB_jr(JR3), .FWD_A(FwdA), .FWD_B(FwdB));
  EX_Mem ex_mem_1 (
    .SET(SET_1), .SSET(SSET_1), .MemToReg(MemToReg_1), .RegWr(RegWr_1), .R7(R7_1), .MemRd(MemRd_1),
    .MemWr(MemWr_1), .Result(alu_1_result), .BusB(BusB_1), .Rd(Rd_1), .Imm8(Imm8_1), .PC_1(jal_jalr__v___1),
    .SET_2(SET_2), .SSET_2(SSET_2), .MemToReg_2(MemToReg_2), .RegWr_2(RegWr_2), .R7_2(R7_2),
    .MemRd_2(MemRd_2), .MemWr_2(MemWr_2), .Result_2(ALU_result_2), .BusB_2(ex_mem_1_busb_2), .Rd_2(Rd_2),
    .Imm8_2(Imm8_2), .PC_1_2(jal_jalr__v_____2), .CLK(CLK), .SSETvalue({alu_1_result[23:0], Imm8_1}),
    .SSETvalue_2(SSET_value_2), .pc_next(pc_next_1), .pc_next_2(pc_next_2), .Imm5(Imm5_1), .Imm5_2(Imm5_2),
    .Imm11(Imm11_1), .Imm11_2(Imm11_2), .Imm(Imm_1), .Imm_2(Imm_2), .clear(clear_3), .opcode(opcode1),
    .opcode_2(opcode2), .J(J_1), .J_2(J_2), .JR(JR_1), .JR_2(JR2));
  Bit_Extender #(.in_width(32), .out_width(20), .\type ("sign")) bit_extender_5 (
    .in(ALU_result_2), .out(bit_extender_5_out));
  assign SET___value_2 = {{24{Imm8_2[7]}}, Imm8_2};  // Bit_Extender bit_extender_6
  RAM #(.addrWidth(20), .dataWidth(32), .bus("separate")) ram_1 (
    .addr(bit_extender_5_out), .din(ex_mem_1_busb_2), .data(ram_1_data), .str(MemWr_2), .sel(1'b1),
    .clk(CLK), .ld(MemRd_2), .clr(in_3));
  Mem_WB mem_wb_1 (
    .SET(SET_2), .SSET(SSET_2), .MemToReg(MemToReg_2), .RegWr(RegWr_2), .R7(R7_2), .SET_2(SET_3),
    .SSET_2(SSET_3), .MemToReg_2(MemToReg_3), .RegWr_2(RegWr_3), .R7_2(R7_3), .Rd(Rd_2), .Rd_2(Rd_3),
    .Result(ALU_result_2), .Result_2(ALU_result_3), .DataRd_2(data_out_of_memory_3), .DataRd(ram_1_data),
    .Imm8(Imm8_2), .Imm8_2(mem_wb_1_imm8_2), .PC_1(jal_jalr__v_____2), .PC_1_2(jal_jalr__v___3),
    .SSETvalue_2(SSET__v___3), .SSETvalue(SSET_value_2), .CLK(CLK), .pc_next(pc_next_2),
    .pc_next_2(pc_next_3), .Imm5(Imm5_2), .Imm5_2(Imm5_3), .Imm11(Imm11_2), .Imm11_2(Imm11_3), .Imm(Imm_2),
    .Imm_2(Imm_3), .clear(clear_2), .opcode(opcode2), .opcode_2(opcode3), .J(J_2), .J_2(J_3), .JR(JR2),
    .JR_2(JR3), .MemRd(MemRd_2), .MemRd_2(MemRd_3));
  assign SET__v___3 = {{24{mem_wb_1_imm8_2[7]}}, mem_wb_1_imm8_2};  // Bit_Extender bit_extender_7
  Multiplexer #(.width(32), .enable("false")) multiplexer_13 (
    .in0(ALU_result_3), .in1(data_out_of_memory_3), .out(multiplexer_13_out), .sel(MemToReg_3));
  Multiplexer #(.width(32), .enable("false")) multiplexer_14 (
    .in0(multiplexer_13_out), .in1(jal_jalr__v___3), .out(multiplexer_14_out), .sel(R7_3));
  Multiplexer #(.width(32), .enable("false")) multiplexer_15 (
    .in0(multiplexer_14_out), .in1(SET__v___3), .out(multiplexer_15_out), .sel(SET_3));
  Multiplexer #(.width(32), .enable("false")) multiplexer_16 (
    .in0(multiplexer_15_out), .in1(SSET__v___3), .out(WB_data), .sel(SSET_3));

  // Other names for the same wires on the sheet: Imm5[1:0] = func; Imm8[4:0] = {Imm5, func};
  //   Imm11[7:0] = {Imm8, Imm5, func}; Rd[2:0] = Imm11

  // Notes on the sheet:
  //   IM
  //   contents of rom_1 (hex, n*v repeats v):
  //   e100 e900 e903 e9e8 e200 ea00 ea03 ea20 e300 eb00 eb00 ebc8 e400 ec00 ec00 ec03 e500 ed00 ed00 ed00
  //   e700 ef00 ef00 ef00 e600 ee00 ee00 ee00 e000 e800 e800 e801 8900 8a01 8b02 74af 8600 ff8 45a1 4001
  //   f7fb
  //   DM
endmodule

module control_unit (
  input  [4:0] Opcode,
  output Reg1,
  output Reg2,
  output Reg3,
  output Ex,
  output Imm,
  output SET,
  output SSET,
  output RegWr,
  output ALUSrc,
  output [4:0] ALUop,
  output MemToReg,
  output MemRd,
  output MemWr,
  output Branch,
  output J,
  output JR,
  output R7,
  output [3:0] PC_NEXT
);

  wire [24:0] AddI, AndI, BEQ, BEQZ, BGEZ, BGTZ, BLEZ, BLTZ, BNEZ, BNQ, EQVI, J_t, JAL, JALR, JR_t, LW, ORI,
       ROR, SEQI, SET_t, SLL, SLTI, SRL, SSET_t, SW, XOR, XORI;

  BEQZ beqz_1 (
    .out_1(BEQZ[0]), .out_2(BEQZ[1]), .out_3(BEQZ[2]), .out_4(BEQZ[3]), .out_5(BEQZ[4]), .out_6(BEQZ[5]),
    .out_7(BEQZ[6]), .out_8(BEQZ[7]), .out_9(BEQZ[8]), .out_10(BEQZ[13:9]), .out_11(BEQZ[14]),
    .out_12(BEQZ[15]), .out_13(BEQZ[16]), .out_14(BEQZ[17]), .out_15(BEQZ[18]), .out_16(BEQZ[19]),
    .out_17(BEQZ[20]), .out_18(BEQZ[24:21]));
  SW sw_1 (
    .out_1(SW[0]), .out_2(SW[1]), .out_3(SW[2]), .out_4(SW[3]), .out_5(SW[4]), .out_6(SW[5]), .out_7(SW[6]),
    .out_8(SW[7]), .out_9(SW[8]), .out_10(SW[13:9]), .out_11(SW[14]), .out_12(SW[15]), .out_13(SW[16]),
    .out_14(SW[17]), .out_15(SW[18]), .out_16(SW[19]), .out_17(SW[20]), .out_18(SW[24:21]));
  JAL jal_1 (
    .out_1(JAL[0]), .out_2(JAL[1]), .out_3(JAL[2]), .out_4(JAL[3]), .out_5(JAL[4]), .out_6(JAL[5]),
    .out_7(JAL[6]), .out_8(JAL[7]), .out_9(JAL[8]), .out_10(JAL[13:9]), .out_11(JAL[14]), .out_12(JAL[15]),
    .out_13(JAL[16]), .out_14(JAL[17]), .out_15(JAL[18]), .out_16(JAL[19]), .out_17(JAL[20]),
    .out_18(JAL[24:21]));
  LW lw_1 (
    .out_1(LW[0]), .out_2(LW[1]), .out_3(LW[2]), .out_4(LW[3]), .out_5(LW[4]), .out_6(LW[5]), .out_7(LW[6]),
    .out_8(LW[7]), .out_9(LW[8]), .out_10(LW[13:9]), .out_11(LW[14]), .out_12(LW[15]), .out_13(LW[16]),
    .out_14(LW[17]), .out_15(LW[18]), .out_16(LW[19]), .out_17(LW[20]), .out_18(LW[24:21]));
  J j_1 (
    .out_1(J_t[0]), .out_2(J_t[1]), .out_3(J_t[2]), .out_4(J_t[3]), .out_5(J_t[4]), .out_6(J_t[5]),
    .out_7(J_t[6]), .out_8(J_t[7]), .out_9(J_t[8]), .out_10(J_t[13:9]), .out_11(J_t[14]), .out_12(J_t[15]),
    .out_13(J_t[16]), .out_14(J_t[17]), .out_15(J_t[18]), .out_16(J_t[19]), .out_17(J_t[20]),
    .out_18(J_t[24:21]));
  BNQ bnq_1 (
    .out_1(BNQ[0]), .out_2(BNQ[1]), .out_3(BNQ[2]), .out_4(BNQ[3]), .out_5(BNQ[4]), .out_6(BNQ[5]),
    .out_7(BNQ[6]), .out_8(BNQ[7]), .out_9(BNQ[8]), .out_10(BNQ[13:9]), .out_11(BNQ[14]), .out_12(BNQ[15]),
    .out_13(BNQ[16]), .out_14(BNQ[17]), .out_15(BNQ[18]), .out_16(BNQ[19]), .out_17(BNQ[20]),
    .out_18(BNQ[24:21]));
  BEQ beq_1 (
    .out_1(BEQ[0]), .out_2(BEQ[1]), .out_3(BEQ[2]), .out_4(BEQ[3]), .out_5(BEQ[4]), .out_6(BEQ[5]),
    .out_7(BEQ[6]), .out_8(BEQ[7]), .out_9(BEQ[8]), .out_10(BEQ[13:9]), .out_11(BEQ[14]), .out_12(BEQ[15]),
    .out_13(BEQ[16]), .out_14(BEQ[17]), .out_15(BEQ[18]), .out_16(BEQ[19]), .out_17(BEQ[20]),
    .out_18(BEQ[24:21]));
  SSET sset_1 (
    .out_1(SSET_t[0]), .out_2(SSET_t[1]), .out_3(SSET_t[2]), .out_4(SSET_t[3]), .out_5(SSET_t[4]),
    .out_6(SSET_t[5]), .out_7(SSET_t[6]), .out_8(SSET_t[7]), .out_9(SSET_t[8]), .out_10(SSET_t[13:9]),
    .out_11(SSET_t[14]), .out_12(SSET_t[15]), .out_13(SSET_t[16]), .out_14(SSET_t[17]), .out_15(SSET_t[18]),
    .out_16(SSET_t[19]), .out_17(SSET_t[20]), .out_18(SSET_t[24:21]));
  ROR ror_1 (
    .out_1(ROR[0]), .out_2(ROR[1]), .out_3(ROR[2]), .out_4(ROR[3]), .out_5(ROR[4]), .out_6(ROR[5]),
    .out_7(ROR[6]), .out_8(ROR[7]), .out_9(ROR[8]), .out_10(ROR[13:9]), .out_11(ROR[14]), .out_12(ROR[15]),
    .out_13(ROR[16]), .out_14(ROR[17]), .out_15(ROR[18]), .out_16(ROR[19]), .out_17(ROR[20]),
    .out_18(ROR[24:21]));
  SET set_1 (
    .out_1(SET_t[0]), .out_2(SET_t[1]), .out_3(SET_t[2]), .out_4(SET_t[3]), .out_5(SET_t[4]),
    .out_6(SET_t[5]), .out_7(SET_t[6]), .out_8(SET_t[7]), .out_9(SET_t[8]), .out_10(SET_t[13:9]),
    .out_11(SET_t[14]), .out_12(SET_t[15]), .out_13(SET_t[16]), .out_14(SET_t[17]), .out_15(SET_t[18]),
    .out_16(SET_t[19]), .out_17(SET_t[20]), .out_18(SET_t[24:21]));
  SRL srl_1 (
    .out_1(SRL[0]), .out_2(SRL[1]), .out_3(SRL[2]), .out_4(SRL[3]), .out_5(SRL[4]), .out_6(SRL[5]),
    .out_7(SRL[6]), .out_8(SRL[7]), .out_9(SRL[8]), .out_10(SRL[13:9]), .out_11(SRL[14]), .out_12(SRL[15]),
    .out_13(SRL[16]), .out_14(SRL[17]), .out_15(SRL[18]), .out_16(SRL[19]), .out_17(SRL[20]),
    .out_18(SRL[24:21]));
  SLL sll_1 (
    .out_1(SLL[0]), .out_2(SLL[1]), .out_3(SLL[2]), .out_4(SLL[3]), .out_5(SLL[4]), .out_6(SLL[5]),
    .out_7(SLL[6]), .out_8(SLL[7]), .out_9(SLL[8]), .out_10(SLL[13:9]), .out_11(SLL[14]), .out_12(SLL[15]),
    .out_13(SLL[16]), .out_14(SLL[17]), .out_15(SLL[18]), .out_16(SLL[19]), .out_17(SLL[20]),
    .out_18(SLL[24:21]));
  JALR jalr_1 (
    .out_1(JALR[0]), .out_2(JALR[1]), .out_3(JALR[2]), .out_4(JALR[3]), .out_5(JALR[4]), .out_6(JALR[5]),
    .out_7(JALR[6]), .out_8(JALR[7]), .out_9(JALR[8]), .out_10(JALR[13:9]), .out_11(JALR[14]),
    .out_12(JALR[15]), .out_13(JALR[16]), .out_14(JALR[17]), .out_15(JALR[18]), .out_16(JALR[19]),
    .out_17(JALR[20]), .out_18(JALR[24:21]));
  SEQI seqi_1 (
    .out_1(SEQI[0]), .out_2(SEQI[1]), .out_3(SEQI[2]), .out_4(SEQI[3]), .out_5(SEQI[4]), .out_6(SEQI[5]),
    .out_7(SEQI[6]), .out_8(SEQI[7]), .out_9(SEQI[8]), .out_10(SEQI[13:9]), .out_11(SEQI[14]),
    .out_12(SEQI[15]), .out_13(SEQI[16]), .out_14(SEQI[17]), .out_15(SEQI[18]), .out_16(SEQI[19]),
    .out_17(SEQI[20]), .out_18(SEQI[24:21]));
  JR jr_1 (
    .out_1(JR_t[0]), .out_2(JR_t[1]), .out_3(JR_t[2]), .out_4(JR_t[3]), .out_5(JR_t[4]), .out_6(JR_t[5]),
    .out_7(JR_t[6]), .out_8(JR_t[7]), .out_9(JR_t[8]), .out_10(JR_t[13:9]), .out_11(JR_t[14]),
    .out_12(JR_t[15]), .out_13(JR_t[16]), .out_14(JR_t[17]), .out_15(JR_t[18]), .out_16(JR_t[19]),
    .out_17(JR_t[20]), .out_18(JR_t[24:21]));
  Multiplexer #(.select(5), .width(25), .enable("false")) multiplexer_1 (
    .in0(25'h80), .in1(25'h280), .in2({25{1'b0}}), .in3({25{1'b0}}), .in4(AndI), .in5(ORI), .in6(XORI),
    .in7(EQVI), .in8(AddI), .in9(SLTI), .in10(SEQI), .in11(SLL), .in12(SRL), .in13(ROR), .in14(BEQ),
    .in15(BNQ), .in16(LW), .in17(SW), .in18({25{1'b0}}), .in19({25{1'b0}}), .in20(BEQZ), .in21(BNEZ),
    .in22(BLTZ), .in23(BGEZ), .in24(BGTZ), .in25(BLEZ), .in26(JR_t), .in27(JALR), .in28(SET_t),
    .in29(SSET_t), .in30(J_t), .in31(JAL),
    .out({PC_NEXT, R7, JR, J, Branch, MemWr, MemRd, MemToReg, ALUop, ALUSrc, RegWr, SSET, SET, Imm, Ex, Reg3, Reg2, Reg1}),
    .sel(Opcode));
  SLTI slti_1 (
    .out_1(SLTI[0]), .out_2(SLTI[1]), .out_3(SLTI[2]), .out_4(SLTI[3]), .out_5(SLTI[4]), .out_6(SLTI[5]),
    .out_7(SLTI[6]), .out_8(SLTI[7]), .out_9(SLTI[8]), .out_10(SLTI[13:9]), .out_11(SLTI[14]),
    .out_12(SLTI[15]), .out_13(SLTI[16]), .out_14(SLTI[17]), .out_15(SLTI[18]), .out_16(SLTI[19]),
    .out_17(SLTI[20]), .out_18(SLTI[24:21]));
  BLEZ blez_1 (
    .out_1(BLEZ[0]), .out_2(BLEZ[1]), .out_3(BLEZ[2]), .out_4(BLEZ[3]), .out_5(BLEZ[4]), .out_6(BLEZ[5]),
    .out_7(BLEZ[6]), .out_8(BLEZ[7]), .out_9(BLEZ[8]), .out_10(BLEZ[13:9]), .out_11(BLEZ[14]),
    .out_12(BLEZ[15]), .out_13(BLEZ[16]), .out_14(BLEZ[17]), .out_15(BLEZ[18]), .out_16(BLEZ[19]),
    .out_17(BLEZ[20]), .out_18(BLEZ[24:21]));
  AddI addi_1 (
    .out_1(AddI[0]), .out_2(AddI[1]), .out_3(AddI[2]), .out_4(AddI[3]), .out_5(AddI[4]), .out_6(AddI[5]),
    .out_7(AddI[6]), .out_8(AddI[7]), .out_9(AddI[8]), .out_10(AddI[13:9]), .out_11(AddI[14]),
    .out_12(AddI[15]), .out_13(AddI[16]), .out_14(AddI[17]), .out_15(AddI[18]), .out_16(AddI[19]),
    .out_17(AddI[20]), .out_18(AddI[24:21]));
  EQVI eqvi_1 (
    .out_1(EQVI[0]), .out_2(EQVI[1]), .out_3(EQVI[2]), .out_4(EQVI[3]), .out_5(EQVI[4]), .out_6(EQVI[5]),
    .out_7(EQVI[6]), .out_8(EQVI[7]), .out_9(EQVI[8]), .out_10(EQVI[13:9]), .out_11(EQVI[14]),
    .out_12(EQVI[15]), .out_13(EQVI[16]), .out_14(EQVI[17]), .out_15(EQVI[18]), .out_16(EQVI[19]),
    .out_17(EQVI[20]), .out_18(EQVI[24:21]));
  BGTZ bgtz_1 (
    .out_1(BGTZ[0]), .out_2(BGTZ[1]), .out_3(BGTZ[2]), .out_4(BGTZ[3]), .out_5(BGTZ[4]), .out_6(BGTZ[5]),
    .out_7(BGTZ[6]), .out_8(BGTZ[7]), .out_9(BGTZ[8]), .out_10(BGTZ[13:9]), .out_11(BGTZ[14]),
    .out_12(BGTZ[15]), .out_13(BGTZ[16]), .out_14(BGTZ[17]), .out_15(BGTZ[18]), .out_16(BGTZ[19]),
    .out_17(BGTZ[20]), .out_18(BGTZ[24:21]));
  XORI xori_1 (
    .out_1(XOR[0]), .out_2(XOR[1]), .out_3(XOR[2]), .out_4(XOR[3]), .out_5(XOR[4]), .out_6(XOR[5]),
    .out_7(XOR[6]), .out_8(XOR[7]), .out_9(XOR[8]), .out_10(XOR[13:9]), .out_11(XOR[14]), .out_12(XOR[15]),
    .out_13(XOR[16]), .out_14(XOR[17]), .out_15(XOR[18]), .out_16(XOR[19]), .out_17(XOR[20]),
    .out_18(XOR[24:21]));
  BGEZ bgez_1 (
    .out_1(BGEZ[0]), .out_2(BGEZ[1]), .out_3(BGEZ[2]), .out_4(BGEZ[3]), .out_5(BGEZ[4]), .out_6(BGEZ[5]),
    .out_7(BGEZ[6]), .out_8(BGEZ[7]), .out_9(BGEZ[8]), .out_10(BGEZ[13:9]), .out_11(BGEZ[14]),
    .out_12(BGEZ[15]), .out_13(BGEZ[16]), .out_14(BGEZ[17]), .out_15(BGEZ[18]), .out_16(BGEZ[19]),
    .out_17(BGEZ[20]), .out_18(BGEZ[24:21]));
  ORI ori_1 (
    .out_1(ORI[0]), .out_2(ORI[1]), .out_3(ORI[2]), .out_4(ORI[3]), .out_5(ORI[4]), .out_6(ORI[5]),
    .out_7(ORI[6]), .out_8(ORI[7]), .out_9(ORI[8]), .out_10(ORI[13:9]), .out_11(ORI[14]), .out_12(ORI[15]),
    .out_13(ORI[16]), .out_14(ORI[17]), .out_15(ORI[18]), .out_16(ORI[19]), .out_17(ORI[20]),
    .out_18(ORI[24:21]));
  BLTZ bltz_1 (
    .out_1(BLTZ[0]), .out_2(BLTZ[1]), .out_3(BLTZ[2]), .out_4(BLTZ[3]), .out_5(BLTZ[4]), .out_6(BLTZ[5]),
    .out_7(BLTZ[6]), .out_8(BLTZ[7]), .out_9(BLTZ[8]), .out_10(BLTZ[13:9]), .out_11(BLTZ[14]),
    .out_12(BLTZ[15]), .out_13(BLTZ[16]), .out_14(BLTZ[17]), .out_15(BLTZ[18]), .out_16(BLTZ[19]),
    .out_17(BLTZ[20]), .out_18(BLTZ[24:21]));
  AndI andi_1 (
    .out_1(AndI[0]), .out_2(AndI[1]), .out_3(AndI[2]), .out_4(AndI[3]), .out_5(AndI[4]), .out_6(AndI[5]),
    .out_7(AndI[6]), .out_8(AndI[7]), .out_9(AndI[8]), .out_10(AndI[13:9]), .out_11(AndI[14]),
    .out_12(AndI[15]), .out_13(AndI[16]), .out_14(AndI[17]), .out_15(AndI[18]), .out_16(AndI[19]),
    .out_17(AndI[20]), .out_18(AndI[24:21]));
  BNEZ bnez_1 (
    .out_1(BNEZ[0]), .out_2(BNEZ[1]), .out_3(BNEZ[2]), .out_4(BNEZ[3]), .out_5(BNEZ[4]), .out_6(BNEZ[5]),
    .out_7(BNEZ[6]), .out_8(BNEZ[7]), .out_9(BNEZ[8]), .out_10(BNEZ[13:9]), .out_11(BNEZ[14]),
    .out_12(BNEZ[15]), .out_13(BNEZ[16]), .out_14(BNEZ[17]), .out_15(BNEZ[18]), .out_16(BNEZ[19]),
    .out_17(BNEZ[20]), .out_18(BNEZ[24:21]));
endmodule

module PC (
  input  [19:0] Pc,
  input  [19:0] Pc_IF_ID,
  input  [4:0] offset_1_imm5,
  input  [7:0] Offset2_imm8,
  input  Imm,
  input  [10:0] Jumb_imm11,
  input  beqz,
  input  [3:0] PC_Next,
  input  beq,
  input  bneq,
  input  bnez,
  input  bltz,
  input  bgez,
  input  bgtz,
  input  [31:0] Reg_Rd,
  input  blez,
  input  Branch,
  input  J,
  input  JR,
  output [19:0] NPC
);

  wire and_1_out, and_2_out, and_3_out, and_4_out, and_5_out, and_6_out, and_7_out, and_8_out;
  wire [19:0] adder_1_out, adder_2_out, adder_3_out, adder_4_out, bit_extender_1_out, bit_extender_2_out,
       bit_extender_3_out, multiplexer_1_out, multiplexer_2_out, multiplexer_3_out, multiplexer_4_out,
       multiplexer_5_out, multiplexer_6_out, multiplexer_7_out, multiplexer_8_out, multiplexer_9_out,
       multiplexer_10_out, multiplexer_12_out;

  assign bit_extender_1_out = {{15{offset_1_imm5[4]}}, offset_1_imm5};  // Bit_Extender bit_extender_1
  assign bit_extender_2_out = {{12{Offset2_imm8[7]}}, Offset2_imm8};  // Bit_Extender bit_extender_2
  Multiplexer #(.width(20), .enable("false")) multiplexer_1 (
    .in0(bit_extender_1_out), .in1(bit_extender_2_out), .out(multiplexer_1_out), .sel(Imm));
  assign bit_extender_3_out = {{9{Jumb_imm11[10]}}, Jumb_imm11};  // Bit_Extender bit_extender_3
  Adder #(.width(20)) adder_1 (.a(Pc), .b(20'h1), .out(adder_1_out));  // open: cin, cout
  Adder #(.width(20)) adder_2 (.a(Pc_IF_ID), .b(multiplexer_1_out), .out(adder_2_out));  // open: cin, cout
  Adder #(.width(20)) adder_3 (.a(Pc_IF_ID), .b(bit_extender_3_out), .out(adder_3_out));  // open: cin, cout
  Adder #(.width(20)) adder_4 (.a(multiplexer_1_out), .b(Reg_Rd[19:0]), .out(adder_4_out));  // open: cin, cout
  Multiplexer #(.width(20), .enable("false")) multiplexer_2 (
    .in0(adder_1_out), .in1(adder_2_out), .out(multiplexer_2_out), .sel(and_1_out));
  and and_1 (and_1_out, Branch, beq);
  Multiplexer #(.width(20), .enable("false")) multiplexer_3 (
    .in0(adder_1_out), .in1(adder_2_out), .out(multiplexer_3_out), .sel(and_2_out));
  and and_2 (and_2_out, Branch, bneq);
  and and_3 (and_3_out, Branch, beqz);
  Multiplexer #(.width(20), .enable("false")) multiplexer_4 (
    .in0(adder_1_out), .in1(adder_2_out), .out(multiplexer_4_out), .sel(and_3_out));
  and and_4 (and_4_out, Branch, bnez);
  Multiplexer #(.width(20), .enable("false")) multiplexer_5 (
    .in0(adder_1_out), .in1(adder_2_out), .out(multiplexer_5_out), .sel(and_4_out));
  and and_5 (and_5_out, Branch, bltz);
  Multiplexer #(.width(20), .enable("false")) multiplexer_6 (
    .in0(adder_1_out), .in1(adder_2_out), .out(multiplexer_6_out), .sel(and_5_out));
  and and_6 (and_6_out, Branch, bgez);
  Multiplexer #(.width(20), .enable("false")) multiplexer_7 (
    .in0(adder_1_out), .in1(adder_2_out), .out(multiplexer_7_out), .sel(and_6_out));
  and and_7 (and_7_out, Branch, bgtz);
  Multiplexer #(.width(20), .enable("false")) multiplexer_8 (
    .in0(adder_1_out), .in1(adder_2_out), .out(multiplexer_8_out), .sel(and_7_out));
  and and_8 (and_8_out, Branch, blez);
  Multiplexer #(.width(20), .enable("false")) multiplexer_9 (
    .in0(adder_1_out), .in1(adder_2_out), .out(multiplexer_9_out), .sel(and_8_out));
  Multiplexer #(.width(20), .enable("false")) multiplexer_10 (
    .in0(adder_1_out), .in1(adder_3_out), .out(multiplexer_10_out), .sel(J));
  Multiplexer #(.select(4), .width(20)) multiplexer_11 (
    .in0(multiplexer_2_out), .in1(multiplexer_3_out), .in2(multiplexer_4_out), .in3(multiplexer_5_out),
    .in4(multiplexer_6_out), .in5(multiplexer_7_out), .in6(multiplexer_8_out), .in7(multiplexer_9_out),
    .in8(multiplexer_10_out), .in9(multiplexer_12_out), .out(NPC), .sel(PC_Next));  // open: in10, in11, in12, in13, in14, in15, en
  Multiplexer #(.width(20), .enable("false")) multiplexer_12 (
    .in0(adder_1_out), .in1(adder_4_out), .out(multiplexer_12_out), .sel(JR));
endmodule

module register__file (
  input  RegWr,
  input  [2:0] Rs,
  input  [2:0] Rt,
  input  [2:0] Rd,
  input  CLK,
  input  clear,
  input  [31:0] bus_w,
  output [31:0] bus_A,
  output [31:0] bus_B
);

  wire decoder_1_out0, decoder_1_out1, decoder_1_out2, decoder_1_out3, decoder_1_out4, decoder_1_out5,
       decoder_1_out6, decoder_1_out7;
  wire [31:0] register_1_q, register_2_q, register_3_q, register_4_q, register_5_q, register_6_q,
       register_7_q, register_8_q;

  Decoder #(.select(3), .disabled(0)) decoder_1 (
    .out0(decoder_1_out0), .out1(decoder_1_out1), .out2(decoder_1_out2), .out3(decoder_1_out3),
    .out4(decoder_1_out4), .out5(decoder_1_out5), .out6(decoder_1_out6), .out7(decoder_1_out7), .sel(Rd),
    .en(RegWr));
  Register #(.width(32), .trigger("high")) register_1 (
    .D(bus_w), .en(decoder_1_out0), .Q(register_1_q), .clk(CLK), .clr(clear));
  Register #(.width(32), .trigger("high")) register_2 (
    .D(bus_w), .en(decoder_1_out1), .Q(register_2_q), .clk(CLK), .clr(clear));
  Register #(.width(32), .trigger("high")) register_3 (
    .D(bus_w), .en(decoder_1_out2), .Q(register_3_q), .clk(CLK), .clr(clear));
  Register #(.width(32), .trigger("high")) register_4 (
    .D(bus_w), .en(decoder_1_out3), .Q(register_4_q), .clk(CLK), .clr(clear));
  Register #(.width(32), .trigger("high")) register_5 (
    .D(bus_w), .en(decoder_1_out4), .Q(register_5_q), .clk(CLK), .clr(clear));
  Register #(.width(32), .trigger("high")) register_6 (
    .D(bus_w), .en(decoder_1_out5), .Q(register_6_q), .clk(CLK), .clr(clear));
  Register #(.width(32), .trigger("high")) register_7 (
    .D(bus_w), .en(decoder_1_out6), .Q(register_7_q), .clk(CLK), .clr(clear));
  Register #(.width(32), .trigger("high")) register_8 (
    .D(bus_w), .en(decoder_1_out7), .Q(register_8_q), .clk(CLK), .clr(clear));
  Multiplexer #(.select(3), .width(32), .enable("false")) multiplexer_1 (
    .in0(register_1_q), .in1(register_2_q), .in2(register_3_q), .in3(register_4_q), .in4(register_5_q),
    .in5(register_6_q), .in6(register_7_q), .in7(register_8_q), .out(bus_A), .sel(Rs));
  Multiplexer #(.select(3), .width(32), .enable("false")) multiplexer_2 (
    .in0(register_1_q), .in1(register_2_q), .in2(register_3_q), .in3(register_4_q), .in4(register_5_q),
    .in5(register_6_q), .in6(register_7_q), .in7(register_8_q), .out(bus_B), .sel(Rt));
endmodule

module ALU (
  input  [1:0] func,
  input  [4:0] ALUop,
  input  [31:0] in_3,
  input  [31:0] in_4,
  output [31:0] result
);

  wire comparator_1_eq, comparator_1_lt;
  wire [31:0] adder_1_out, and_1_out, bit_extender_1_out, bit_extender_2_out, multiplexer_1_out,
       multiplexer_2_out, or_1_out, shifter_1_out, shifter_2_out, shifter_3_out, subtractor_1_out,
       xnor_1_out, xor_1_out;

  Adder #(.width(32)) adder_1 (.a(in_3), .b(in_4), .out(adder_1_out));  // open: cin, cout
  Subtractor #(.width(32)) subtractor_1 (.a(in_3), .b(in_4), .out(subtractor_1_out));  // open: bin, bout
  Comparator #(.width(32)) comparator_1 (.a(in_3), .b(in_4), .eq(comparator_1_eq), .lt(comparator_1_lt));  // open: gt
  Shifter #(.width(32)) shifter_1 (.in(in_3), .\dist (in_4[4:0]), .out(shifter_1_out));
  Shifter #(.width(32), .shift("lr")) shifter_2 (.in(in_3), .\dist (in_4[4:0]), .out(shifter_2_out));
  Shifter #(.width(32), .shift("rr")) shifter_3 (.in(in_3), .\dist (in_4[4:0]), .out(shifter_3_out));
  assign and_1_out = in_3 & in_4;  // AND_Gate and_1, 32 bits wide
  assign bit_extender_1_out = {{31{1'b0}}, comparator_1_lt};  // Bit_Extender bit_extender_1
  assign bit_extender_2_out = {{31{1'b0}}, comparator_1_eq};  // Bit_Extender bit_extender_2
  assign or_1_out = in_3 | in_4;  // OR_Gate or_1, 32 bits wide
  assign xor_1_out = in_3 ^ in_4;  // XOR_Gate xor_1, 32 bits wide
  assign xnor_1_out = ~(in_3 ^ in_4);  // XNOR_Gate xnor_1, 32 bits wide
  Multiplexer #(.select(2), .width(32), .enable("false")) multiplexer_1 (
    .in0(and_1_out), .in1(or_1_out), .in2(xor_1_out), .in3(xnor_1_out), .out(multiplexer_1_out), .sel(func));
  Multiplexer #(.select(2), .width(32), .enable("false")) multiplexer_2 (
    .in0(adder_1_out), .in1(subtractor_1_out), .in2(bit_extender_1_out), .in3(bit_extender_2_out),
    .out(multiplexer_2_out), .sel(func));
  Multiplexer #(.select(5), .width(32), .enable("false")) multiplexer_3 (
    .in0(multiplexer_1_out), .in1(multiplexer_2_out), .in2(and_1_out), .in3(or_1_out), .in4(xor_1_out),
    .in5(xnor_1_out), .in6(adder_1_out), .in7({32{1'b0}}), .in8({32{1'b0}}), .in9(shifter_1_out),
    .in10(shifter_2_out), .in11(shifter_3_out), .in12({32{1'b0}}), .in13({32{1'b0}}), .in14(adder_1_out),
    .in15(adder_1_out), .in16({32{1'b0}}), .in17({32{1'b0}}), .in18({32{1'b0}}), .in19({32{1'b0}}),
    .in20({32{1'b0}}), .in21({32{1'b0}}), .in22({32{1'b0}}), .in23({32{1'b0}}), .in24({32{1'b0}}),
    .in25(in_3), .in26({32{1'b0}}), .in27({32{1'b0}}), .in28({32{1'b0}}), .in29({32{1'b0}}),
    .in30({32{1'b0}}), .in31({32{1'b0}}), .out(result), .sel(ALUop));

  // Other names for the same wires on the sheet: A[31:0] = in_3; B[31:0] = in_4
endmodule

module AndI (
  output out_1,
  output out_2,
  output out_3,
  output out_4,
  output out_5,
  output out_6,
  output out_7,
  output out_8,
  output out_9,
  output [4:0] out_10,
  output out_11,
  output out_12,
  output out_13,
  output out_14,
  output out_15,
  output out_16,
  output out_17,
  output [3:0] out_18
);


  assign out_1 = 1'b0;
  assign out_2 = 1'b0;
  assign out_3 = 1'b0;
  assign out_4 = 1'b0;
  assign out_5 = 1'b0;
  assign out_6 = 1'b0;
  assign out_7 = 1'b0;
  assign out_8 = 1'b1;
  assign out_9 = 1'b1;
  assign out_10 = 5'b00010;
  assign out_11 = 1'b0;
  assign out_12 = 1'b0;
  assign out_13 = 1'b0;
  assign out_14 = 1'b0;
  assign out_15 = 1'b0;
  assign out_16 = 1'b0;
  assign out_17 = 1'b0;
  assign out_18 = 4'b0000;

  // Notes on the sheet:
  //   MemRd
  //   MemWr
  //   Branch
  //   J
  //   JR
  //   pc next
  //   Reg1
  //   Reg2
  //   Reg3
  //   EX
  //   Imm
  //   SET
  //   SSET
  //   RegWr
  //   ALUSrc
  //   ALUop
  //   MemToReg
  //   R7
endmodule

module ORI (
  output out_1,
  output out_2,
  output out_3,
  output out_4,
  output out_5,
  output out_6,
  output out_7,
  output out_8,
  output out_9,
  output [4:0] out_10,
  output out_11,
  output out_12,
  output out_13,
  output out_14,
  output out_15,
  output out_16,
  output out_17,
  output [3:0] out_18
);


  assign out_1 = 1'b0;
  assign out_2 = 1'b0;
  assign out_3 = 1'b0;
  assign out_4 = 1'b0;
  assign out_5 = 1'b0;
  assign out_6 = 1'b0;
  assign out_7 = 1'b0;
  assign out_8 = 1'b1;
  assign out_9 = 1'b1;
  assign out_10 = 5'b00011;
  assign out_11 = 1'b0;
  assign out_12 = 1'b0;
  assign out_13 = 1'b0;
  assign out_14 = 1'b0;
  assign out_15 = 1'b0;
  assign out_16 = 1'b0;
  assign out_17 = 1'b0;
  assign out_18 = 4'b0000;

  // Notes on the sheet:
  //   MemToReg
  //   MemRd
  //   MemWr
  //   Branch
  //   J
  //   JR
  //   pc next
  //   Reg1
  //   Reg2
  //   Reg3
  //   EX
  //   Imm
  //   SET
  //   SSET
  //   RegWr
  //   ALUSrc
  //   ALUop
  //   R7
endmodule

module XORI (
  output out_1,
  output out_2,
  output out_3,
  output out_4,
  output out_5,
  output out_6,
  output out_7,
  output out_8,
  output out_9,
  output [4:0] out_10,
  output out_11,
  output out_12,
  output out_13,
  output out_14,
  output out_15,
  output out_16,
  output out_17,
  output [3:0] out_18
);


  assign out_1 = 1'b0;
  assign out_2 = 1'b0;
  assign out_3 = 1'b0;
  assign out_4 = 1'b0;
  assign out_5 = 1'b0;
  assign out_6 = 1'b0;
  assign out_7 = 1'b0;
  assign out_8 = 1'b1;
  assign out_9 = 1'b1;
  assign out_10 = 5'b00100;
  assign out_11 = 1'b0;
  assign out_12 = 1'b0;
  assign out_13 = 1'b0;
  assign out_14 = 1'b0;
  assign out_15 = 1'b0;
  assign out_16 = 1'b0;
  assign out_17 = 1'b0;
  assign out_18 = 4'b0000;

  // Notes on the sheet:
  //   Reg2
  //   EX
  //   Imm
  //   SET
  //   SSET
  //   RegWr
  //   ALUSrc
  //   ALUop
  //   MemToReg
  //   MemRd
  //   MemWr
  //   Branch
  //   J
  //   JR
  //   R7
  //   pc next
  //   Reg1
  //   Reg3
endmodule

module EQVI (
  output out_1,
  output out_2,
  output out_3,
  output out_4,
  output out_5,
  output out_6,
  output out_7,
  output out_8,
  output out_9,
  output [4:0] out_10,
  output out_11,
  output out_12,
  output out_13,
  output out_14,
  output out_15,
  output out_16,
  output out_17,
  output [3:0] out_18
);


  assign out_1 = 1'b0;
  assign out_2 = 1'b0;
  assign out_3 = 1'b0;
  assign out_4 = 1'b0;
  assign out_5 = 1'b0;
  assign out_6 = 1'b0;
  assign out_7 = 1'b0;
  assign out_8 = 1'b1;
  assign out_9 = 1'b1;
  assign out_10 = 5'b00101;
  assign out_11 = 1'b0;
  assign out_12 = 1'b0;
  assign out_13 = 1'b0;
  assign out_14 = 1'b0;
  assign out_15 = 1'b0;
  assign out_16 = 1'b0;
  assign out_17 = 1'b0;
  assign out_18 = 4'b0000;

  // Notes on the sheet:
  //   Reg2
  //   EX
  //   Imm
  //   SET
  //   SSET
  //   RegWr
  //   ALUSrc
  //   ALUop
  //   MemToReg
  //   MemRd
  //   MemWr
  //   Branch
  //   J
  //   JR
  //   R7
  //   pc next
  //   Reg1
  //   Reg3
endmodule

module AddI (
  output out_1,
  output out_2,
  output out_3,
  output out_4,
  output out_5,
  output out_6,
  output out_7,
  output out_8,
  output out_9,
  output [4:0] out_10,
  output out_11,
  output out_12,
  output out_13,
  output out_14,
  output out_15,
  output out_16,
  output out_17,
  output [3:0] out_18
);


  assign out_1 = 1'b0;
  assign out_2 = 1'b0;
  assign out_3 = 1'b0;
  assign out_4 = 1'b1;
  assign out_5 = 1'b0;
  assign out_6 = 1'b0;
  assign out_7 = 1'b0;
  assign out_8 = 1'b1;
  assign out_9 = 1'b1;
  assign out_10 = 5'b00110;
  assign out_11 = 1'b0;
  assign out_12 = 1'b0;
  assign out_13 = 1'b0;
  assign out_14 = 1'b0;
  assign out_15 = 1'b0;
  assign out_16 = 1'b0;
  assign out_17 = 1'b0;
  assign out_18 = 4'b0000;

  // Notes on the sheet:
  //   Reg2
  //   EX
  //   Imm
  //   SET
  //   SSET
  //   RegWr
  //   ALUSrc
  //   ALUop
  //   MemToReg
  //   MemRd
  //   MemWr
  //   Branch
  //   J
  //   JR
  //   R7
  //   pc next
  //   Reg1
  //   Reg3
endmodule

module SLTI (
  output out_1,
  output out_2,
  output out_3,
  output out_4,
  output out_5,
  output out_6,
  output out_7,
  output out_8,
  output out_9,
  output [4:0] out_10,
  output out_11,
  output out_12,
  output out_13,
  output out_14,
  output out_15,
  output out_16,
  output out_17,
  output [3:0] out_18
);


  assign out_1 = 1'b0;
  assign out_2 = 1'b0;
  assign out_3 = 1'b0;
  assign out_4 = 1'b1;
  assign out_5 = 1'b0;
  assign out_6 = 1'b0;
  assign out_7 = 1'b0;
  assign out_8 = 1'b1;
  assign out_9 = 1'b1;
  assign out_10 = 5'b00111;
  assign out_11 = 1'b0;
  assign out_12 = 1'b0;
  assign out_13 = 1'b0;
  assign out_14 = 1'b0;
  assign out_15 = 1'b0;
  assign out_16 = 1'b0;
  assign out_17 = 1'b0;
  assign out_18 = 4'b0000;

  // Notes on the sheet:
  //   Reg2
  //   EX
  //   Imm
  //   SET
  //   SSET
  //   RegWr
  //   ALUSrc
  //   ALUop
  //   MemToReg
  //   MemRd
  //   MemWr
  //   Branch
  //   J
  //   JR
  //   R7
  //   pc next
  //   Reg1
  //   Reg3
endmodule

module SEQI (
  output out_1,
  output out_2,
  output out_3,
  output out_4,
  output out_5,
  output out_6,
  output out_7,
  output out_8,
  output out_9,
  output [4:0] out_10,
  output out_11,
  output out_12,
  output out_13,
  output out_14,
  output out_15,
  output out_16,
  output out_17,
  output [3:0] out_18
);


  assign out_1 = 1'b0;
  assign out_2 = 1'b0;
  assign out_3 = 1'b0;
  assign out_4 = 1'b1;
  assign out_5 = 1'b0;
  assign out_6 = 1'b0;
  assign out_7 = 1'b0;
  assign out_8 = 1'b1;
  assign out_9 = 1'b1;
  assign out_10 = 5'b01000;
  assign out_11 = 1'b0;
  assign out_12 = 1'b0;
  assign out_13 = 1'b0;
  assign out_14 = 1'b0;
  assign out_15 = 1'b0;
  assign out_16 = 1'b0;
  assign out_17 = 1'b0;
  assign out_18 = 4'b0000;

  // Notes on the sheet:
  //   Reg2
  //   EX
  //   Imm
  //   SET
  //   SSET
  //   RegWr
  //   ALUSrc
  //   ALUop
  //   MemToReg
  //   MemRd
  //   MemWr
  //   Branch
  //   J
  //   JR
  //   R7
  //   pc next
  //   Reg1
  //   Reg3
endmodule

module SLL (
  output out_1,
  output out_2,
  output out_3,
  output out_4,
  output out_5,
  output out_6,
  output out_7,
  output out_8,
  output out_9,
  output [4:0] out_10,
  output out_11,
  output out_12,
  output out_13,
  output out_14,
  output out_15,
  output out_16,
  output out_17,
  output [3:0] out_18
);


  assign out_1 = 1'b0;
  assign out_2 = 1'b0;
  assign out_3 = 1'b0;
  assign out_4 = 1'b0;
  assign out_5 = 1'b0;
  assign out_6 = 1'b0;
  assign out_7 = 1'b0;
  assign out_8 = 1'b1;
  assign out_9 = 1'b1;
  assign out_10 = 5'b01001;
  assign out_11 = 1'b0;
  assign out_12 = 1'b0;
  assign out_13 = 1'b0;
  assign out_14 = 1'b0;
  assign out_15 = 1'b0;
  assign out_16 = 1'b0;
  assign out_17 = 1'b0;
  assign out_18 = 4'b0000;

  // Notes on the sheet:
  //   Reg2
  //   EX
  //   Imm
  //   SET
  //   SSET
  //   RegWr
  //   ALUSrc
  //   ALUop
  //   MemToReg
  //   MemRd
  //   MemWr
  //   Branch
  //   J
  //   JR
  //   R7
  //   pc next
  //   Reg1
  //   Reg3
endmodule

module SRL (
  output out_1,
  output out_2,
  output out_3,
  output out_4,
  output out_5,
  output out_6,
  output out_7,
  output out_8,
  output out_9,
  output [4:0] out_10,
  output out_11,
  output out_12,
  output out_13,
  output out_14,
  output out_15,
  output out_16,
  output out_17,
  output [3:0] out_18
);


  assign out_1 = 1'b0;
  assign out_2 = 1'b0;
  assign out_3 = 1'b0;
  assign out_4 = 1'b0;
  assign out_5 = 1'b0;
  assign out_6 = 1'b0;
  assign out_7 = 1'b0;
  assign out_8 = 1'b1;
  assign out_9 = 1'b1;
  assign out_10 = 5'b01010;
  assign out_11 = 1'b0;
  assign out_12 = 1'b0;
  assign out_13 = 1'b0;
  assign out_14 = 1'b0;
  assign out_15 = 1'b0;
  assign out_16 = 1'b0;
  assign out_17 = 1'b0;
  assign out_18 = 4'b0000;

  // Notes on the sheet:
  //   Reg2
  //   EX
  //   Imm
  //   SET
  //   SSET
  //   RegWr
  //   ALUSrc
  //   ALUop
  //   MemToReg
  //   MemRd
  //   MemWr
  //   Branch
  //   J
  //   JR
  //   R7
  //   pc next
  //   Reg1
  //   Reg3
endmodule

module ROR (
  output out_1,
  output out_2,
  output out_3,
  output out_4,
  output out_5,
  output out_6,
  output out_7,
  output out_8,
  output out_9,
  output [4:0] out_10,
  output out_11,
  output out_12,
  output out_13,
  output out_14,
  output out_15,
  output out_16,
  output out_17,
  output [3:0] out_18
);


  assign out_1 = 1'b0;
  assign out_2 = 1'b0;
  assign out_3 = 1'b0;
  assign out_4 = 1'b0;
  assign out_5 = 1'b0;
  assign out_6 = 1'b0;
  assign out_7 = 1'b0;
  assign out_8 = 1'b0;
  assign out_9 = 1'b1;
  assign out_10 = 5'b01011;
  assign out_11 = 1'b0;
  assign out_12 = 1'b0;
  assign out_13 = 1'b0;
  assign out_14 = 1'b0;
  assign out_15 = 1'b0;
  assign out_16 = 1'b0;
  assign out_17 = 1'b0;
  assign out_18 = 4'b0000;

  // Notes on the sheet:
  //   Reg2
  //   EX
  //   Imm
  //   SET
  //   SSET
  //   RegWr
  //   ALUSrc
  //   ALUop
  //   MemToReg
  //   MemRd
  //   MemWr
  //   Branch
  //   J
  //   JR
  //   R7
  //   pc next
  //   Reg1
  //   Reg3
endmodule

module BEQ (
  output out_1,
  output out_2,
  output out_3,
  output out_4,
  output out_5,
  output out_6,
  output out_7,
  output out_8,
  output out_9,
  output [4:0] out_10,
  output out_11,
  output out_12,
  output out_13,
  output out_14,
  output out_15,
  output out_16,
  output out_17,
  output [3:0] out_18
);


  assign out_1 = 1'b0;
  assign out_2 = 1'b1;
  assign out_3 = 1'b0;
  assign out_4 = 1'b1;
  assign out_5 = 1'b0;
  assign out_6 = 1'b0;
  assign out_7 = 1'b0;
  assign out_8 = 1'b0;
  assign out_9 = 1'b0;
  assign out_10 = 5'b01100;
  assign out_11 = 1'b0;
  assign out_12 = 1'b0;
  assign out_13 = 1'b0;
  assign out_14 = 1'b1;
  assign out_15 = 1'b0;
  assign out_16 = 1'b0;
  assign out_17 = 1'b0;
  assign out_18 = 4'b0000;

  // Notes on the sheet:
  //   Reg2
  //   EX
  //   Imm
  //   SET
  //   SSET
  //   RegWr
  //   ALUSrc
  //   ALUop
  //   MemToReg
  //   MemRd
  //   MemWr
  //   Branch
  //   J
  //   JR
  //   R7
  //   pc next
  //   Reg1
  //   Reg3
endmodule

module BNQ (
  output out_1,
  output out_2,
  output out_3,
  output out_4,
  output out_5,
  output out_6,
  output out_7,
  output out_8,
  output out_9,
  output [4:0] out_10,
  output out_11,
  output out_12,
  output out_13,
  output out_14,
  output out_15,
  output out_16,
  output out_17,
  output [3:0] out_18
);


  assign out_1 = 1'b0;
  assign out_2 = 1'b1;
  assign out_3 = 1'b0;
  assign out_4 = 1'b1;
  assign out_5 = 1'b0;
  assign out_6 = 1'b0;
  assign out_7 = 1'b0;
  assign out_8 = 1'b0;
  assign out_9 = 1'b0;
  assign out_10 = 5'b01101;
  assign out_11 = 1'b0;
  assign out_12 = 1'b0;
  assign out_13 = 1'b0;
  assign out_14 = 1'b1;
  assign out_15 = 1'b0;
  assign out_16 = 1'b0;
  assign out_17 = 1'b0;
  assign out_18 = 4'b0001;

  // Notes on the sheet:
  //   Reg2
  //   EX
  //   Imm
  //   SET
  //   SSET
  //   RegWr
  //   ALUSrc
  //   ALUop
  //   MemToReg
  //   MemRd
  //   MemWr
  //   Branch
  //   J
  //   JR
  //   R7
  //   pc next
  //   Reg1
  //   Reg3
endmodule

module LW (
  output out_1,
  output out_2,
  output out_3,
  output out_4,
  output out_5,
  output out_6,
  output out_7,
  output out_8,
  output out_9,
  output [4:0] out_10,
  output out_11,
  output out_12,
  output out_13,
  output out_14,
  output out_15,
  output out_16,
  output out_17,
  output [3:0] out_18
);


  assign out_1 = 1'b0;
  assign out_2 = 1'b0;
  assign out_3 = 1'b0;
  assign out_4 = 1'b1;
  assign out_5 = 1'b0;
  assign out_6 = 1'b0;
  assign out_7 = 1'b0;
  assign out_8 = 1'b1;
  assign out_9 = 1'b1;
  assign out_10 = 5'b01110;
  assign out_11 = 1'b1;
  assign out_12 = 1'b1;
  assign out_13 = 1'b0;
  assign out_14 = 1'b0;
  assign out_15 = 1'b0;
  assign out_16 = 1'b0;
  assign out_17 = 1'b0;
  assign out_18 = 4'b0000;

  // Notes on the sheet:
  //   Reg2
  //   EX
  //   Imm
  //   SET
  //   SSET
  //   RegWr
  //   ALUSrc
  //   ALUop
  //   MemToReg
  //   MemRd
  //   MemWr
  //   Branch
  //   J
  //   JR
  //   R7
  //   pc next
  //   Reg1
  //   Reg3
endmodule

module SW (
  output out_1,
  output out_2,
  output out_3,
  output out_4,
  output out_5,
  output out_6,
  output out_7,
  output out_8,
  output out_9,
  output [4:0] out_10,
  output out_11,
  output out_12,
  output out_13,
  output out_14,
  output out_15,
  output out_16,
  output out_17,
  output [3:0] out_18
);


  assign out_1 = 1'b0;
  assign out_2 = 1'b1;
  assign out_3 = 1'b0;
  assign out_4 = 1'b1;
  assign out_5 = 1'b0;
  assign out_6 = 1'b0;
  assign out_7 = 1'b0;
  assign out_8 = 1'b0;
  assign out_9 = 1'b1;
  assign out_10 = 5'b01111;
  assign out_11 = 1'b0;
  assign out_12 = 1'b0;
  assign out_13 = 1'b1;
  assign out_14 = 1'b0;
  assign out_15 = 1'b0;
  assign out_16 = 1'b0;
  assign out_17 = 1'b0;
  assign out_18 = 4'b0000;

  // Notes on the sheet:
  //   Reg2
  //   EX
  //   Imm
  //   SET
  //   SSET
  //   RegWr
  //   ALUSrc
  //   ALUop
  //   MemToReg
  //   MemRd
  //   MemWr
  //   Branch
  //   J
  //   JR
  //   R7
  //   pc next
  //   Reg1
  //   Reg3
endmodule

module BEQZ (
  output out_1,
  output out_2,
  output out_3,
  output out_4,
  output out_5,
  output out_6,
  output out_7,
  output out_8,
  output out_9,
  output [4:0] out_10,
  output out_11,
  output out_12,
  output out_13,
  output out_14,
  output out_15,
  output out_16,
  output out_17,
  output [3:0] out_18
);


  assign out_1 = 1'b0;
  assign out_2 = 1'b1;
  assign out_3 = 1'b0;
  assign out_4 = 1'b1;
  assign out_5 = 1'b1;
  assign out_6 = 1'b0;
  assign out_7 = 1'b0;
  assign out_8 = 1'b0;
  assign out_9 = 1'b1;
  assign out_10 = 5'b10000;
  assign out_11 = 1'b0;
  assign out_12 = 1'b0;
  assign out_13 = 1'b0;
  assign out_14 = 1'b1;
  assign out_15 = 1'b0;
  assign out_16 = 1'b0;
  assign out_17 = 1'b0;
  assign out_18 = 4'b0010;

  // Notes on the sheet:
  //   Reg2
  //   EX
  //   Imm
  //   SET
  //   SSET
  //   RegWr
  //   ALUSrc
  //   ALUop
  //   MemToReg
  //   MemRd
  //   MemWr
  //   Branch
  //   J
  //   JR
  //   R7
  //   pc next
  //   Reg1
  //   Reg3
endmodule

module BNEZ (
  output out_1,
  output out_2,
  output out_3,
  output out_4,
  output out_5,
  output out_6,
  output out_7,
  output out_8,
  output out_9,
  output [4:0] out_10,
  output out_11,
  output out_12,
  output out_13,
  output out_14,
  output out_15,
  output out_16,
  output out_17,
  output [3:0] out_18
);


  assign out_1 = 1'b0;
  assign out_2 = 1'b1;
  assign out_3 = 1'b0;
  assign out_4 = 1'b1;
  assign out_5 = 1'b1;
  assign out_6 = 1'b0;
  assign out_7 = 1'b0;
  assign out_8 = 1'b0;
  assign out_9 = 1'b1;
  assign out_10 = 5'b10001;
  assign out_11 = 1'b0;
  assign out_12 = 1'b0;
  assign out_13 = 1'b0;
  assign out_14 = 1'b1;
  assign out_15 = 1'b0;
  assign out_16 = 1'b0;
  assign out_17 = 1'b0;
  assign out_18 = 4'b0011;

  // Notes on the sheet:
  //   Reg2
  //   EX
  //   Imm
  //   SET
  //   SSET
  //   RegWr
  //   ALUSrc
  //   ALUop
  //   MemToReg
  //   MemRd
  //   MemWr
  //   Branch
  //   J
  //   JR
  //   R7
  //   pc next
  //   Reg1
  //   Reg3
endmodule

module BLTZ (
  output out_1,
  output out_2,
  output out_3,
  output out_4,
  output out_5,
  output out_6,
  output out_7,
  output out_8,
  output out_9,
  output [4:0] out_10,
  output out_11,
  output out_12,
  output out_13,
  output out_14,
  output out_15,
  output out_16,
  output out_17,
  output [3:0] out_18
);


  assign out_1 = 1'b0;
  assign out_2 = 1'b1;
  assign out_3 = 1'b0;
  assign out_4 = 1'b1;
  assign out_5 = 1'b1;
  assign out_6 = 1'b0;
  assign out_7 = 1'b0;
  assign out_8 = 1'b0;
  assign out_9 = 1'b1;
  assign out_10 = 5'b10010;
  assign out_11 = 1'b0;
  assign out_12 = 1'b0;
  assign out_13 = 1'b0;
  assign out_14 = 1'b1;
  assign out_15 = 1'b0;
  assign out_16 = 1'b0;
  assign out_17 = 1'b0;
  assign out_18 = 4'b0100;

  // Notes on the sheet:
  //   Reg2
  //   EX
  //   Imm
  //   SET
  //   SSET
  //   RegWr
  //   ALUSrc
  //   ALUop
  //   MemToReg
  //   MemRd
  //   MemWr
  //   Branch
  //   J
  //   JR
  //   R7
  //   pc next
  //   Reg1
  //   Reg3
endmodule

module BGEZ (
  output out_1,
  output out_2,
  output out_3,
  output out_4,
  output out_5,
  output out_6,
  output out_7,
  output out_8,
  output out_9,
  output [4:0] out_10,
  output out_11,
  output out_12,
  output out_13,
  output out_14,
  output out_15,
  output out_16,
  output out_17,
  output [3:0] out_18
);


  assign out_1 = 1'b0;
  assign out_2 = 1'b1;
  assign out_3 = 1'b0;
  assign out_4 = 1'b1;
  assign out_5 = 1'b1;
  assign out_6 = 1'b0;
  assign out_7 = 1'b0;
  assign out_8 = 1'b0;
  assign out_9 = 1'b1;
  assign out_10 = 5'b10011;
  assign out_11 = 1'b0;
  assign out_12 = 1'b0;
  assign out_13 = 1'b0;
  assign out_14 = 1'b1;
  assign out_15 = 1'b0;
  assign out_16 = 1'b0;
  assign out_17 = 1'b0;
  assign out_18 = 4'b0101;

  // Notes on the sheet:
  //   Reg2
  //   EX
  //   Imm
  //   SET
  //   SSET
  //   RegWr
  //   ALUSrc
  //   ALUop
  //   MemToReg
  //   MemRd
  //   MemWr
  //   Branch
  //   J
  //   JR
  //   R7
  //   pc next
  //   Reg1
  //   Reg3
endmodule

module BGTZ (
  output out_1,
  output out_2,
  output out_3,
  output out_4,
  output out_5,
  output out_6,
  output out_7,
  output out_8,
  output out_9,
  output [4:0] out_10,
  output out_11,
  output out_12,
  output out_13,
  output out_14,
  output out_15,
  output out_16,
  output out_17,
  output [3:0] out_18
);


  assign out_1 = 1'b0;
  assign out_2 = 1'b1;
  assign out_3 = 1'b0;
  assign out_4 = 1'b1;
  assign out_5 = 1'b1;
  assign out_6 = 1'b0;
  assign out_7 = 1'b0;
  assign out_8 = 1'b0;
  assign out_9 = 1'b1;
  assign out_10 = 5'b10100;
  assign out_11 = 1'b0;
  assign out_12 = 1'b0;
  assign out_13 = 1'b0;
  assign out_14 = 1'b1;
  assign out_15 = 1'b0;
  assign out_16 = 1'b0;
  assign out_17 = 1'b0;
  assign out_18 = 4'b0110;

  // Notes on the sheet:
  //   Reg2
  //   EX
  //   Imm
  //   SET
  //   SSET
  //   RegWr
  //   ALUSrc
  //   ALUop
  //   MemToReg
  //   MemRd
  //   MemWr
  //   Branch
  //   J
  //   JR
  //   R7
  //   pc next
  //   Reg1
  //   Reg3
endmodule

module BLEZ (
  output out_1,
  output out_2,
  output out_3,
  output out_4,
  output out_5,
  output out_6,
  output out_7,
  output out_8,
  output out_9,
  output [4:0] out_10,
  output out_11,
  output out_12,
  output out_13,
  output out_14,
  output out_15,
  output out_16,
  output out_17,
  output [3:0] out_18
);


  assign out_1 = 1'b0;
  assign out_2 = 1'b1;
  assign out_3 = 1'b0;
  assign out_4 = 1'b1;
  assign out_5 = 1'b1;
  assign out_6 = 1'b0;
  assign out_7 = 1'b0;
  assign out_8 = 1'b0;
  assign out_9 = 1'b1;
  assign out_10 = 5'b10101;
  assign out_11 = 1'b0;
  assign out_12 = 1'b0;
  assign out_13 = 1'b0;
  assign out_14 = 1'b1;
  assign out_15 = 1'b0;
  assign out_16 = 1'b0;
  assign out_17 = 1'b0;
  assign out_18 = 4'b0111;

  // Notes on the sheet:
  //   Reg2
  //   EX
  //   Imm
  //   SET
  //   SSET
  //   RegWr
  //   ALUSrc
  //   ALUop
  //   MemToReg
  //   MemRd
  //   MemWr
  //   Branch
  //   J
  //   JR
  //   R7
  //   pc next
  //   Reg1
  //   Reg3
endmodule

module JR (
  output out_1,
  output out_2,
  output out_3,
  output out_4,
  output out_5,
  output out_6,
  output out_7,
  output out_8,
  output out_9,
  output [4:0] out_10,
  output out_11,
  output out_12,
  output out_13,
  output out_14,
  output out_15,
  output out_16,
  output out_17,
  output [3:0] out_18
);


  assign out_1 = 1'b0;
  assign out_2 = 1'b1;
  assign out_3 = 1'b0;
  assign out_4 = 1'b0;
  assign out_5 = 1'b1;
  assign out_6 = 1'b0;
  assign out_7 = 1'b0;
  assign out_8 = 1'b0;
  assign out_9 = 1'b0;
  assign out_10 = 5'b10110;
  assign out_11 = 1'b0;
  assign out_12 = 1'b0;
  assign out_13 = 1'b0;
  assign out_14 = 1'b0;
  assign out_15 = 1'b0;
  assign out_16 = 1'b1;
  assign out_17 = 1'b0;
  assign out_18 = 4'b1001;

  // Notes on the sheet:
  //   Reg2
  //   EX
  //   Imm
  //   SET
  //   SSET
  //   RegWr
  //   ALUSrc
  //   ALUop
  //   MemToReg
  //   MemRd
  //   MemWr
  //   Branch
  //   J
  //   JR
  //   R7
  //   pc next
  //   Reg1
  //   Reg3
endmodule

module JALR (
  output out_1,
  output out_2,
  output out_3,
  output out_4,
  output out_5,
  output out_6,
  output out_7,
  output out_8,
  output out_9,
  output [4:0] out_10,
  output out_11,
  output out_12,
  output out_13,
  output out_14,
  output out_15,
  output out_16,
  output out_17,
  output [3:0] out_18
);


  assign out_1 = 1'b0;
  assign out_2 = 1'b1;
  assign out_3 = 1'b1;
  assign out_4 = 1'b0;
  assign out_5 = 1'b1;
  assign out_6 = 1'b0;
  assign out_7 = 1'b0;
  assign out_8 = 1'b1;
  assign out_9 = 1'b0;
  assign out_10 = 5'b10111;
  assign out_11 = 1'b0;
  assign out_12 = 1'b0;
  assign out_13 = 1'b0;
  assign out_14 = 1'b0;
  assign out_15 = 1'b0;
  assign out_16 = 1'b1;
  assign out_17 = 1'b1;
  assign out_18 = 4'b1001;

  // Notes on the sheet:
  //   Reg2
  //   EX
  //   Imm
  //   SET
  //   SSET
  //   RegWr
  //   ALUSrc
  //   ALUop
  //   MemToReg
  //   MemRd
  //   MemWr
  //   Branch
  //   J
  //   JR
  //   R7
  //   pc next
  //   Reg1
  //   Reg3
endmodule

module SET (
  output out_1,
  output out_2,
  output out_3,
  output out_4,
  output out_5,
  output out_6,
  output out_7,
  output out_8,
  output out_9,
  output [4:0] out_10,
  output out_11,
  output out_12,
  output out_13,
  output out_14,
  output out_15,
  output out_16,
  output out_17,
  output [3:0] out_18
);


  assign out_1 = 1'b0;
  assign out_2 = 1'b0;
  assign out_3 = 1'b0;
  assign out_4 = 1'b1;
  assign out_5 = 1'b1;
  assign out_6 = 1'b1;
  assign out_7 = 1'b0;
  assign out_8 = 1'b1;
  assign out_9 = 1'b0;
  assign out_10 = 5'b11000;
  assign out_11 = 1'b0;
  assign out_12 = 1'b0;
  assign out_13 = 1'b0;
  assign out_14 = 1'b0;
  assign out_15 = 1'b0;
  assign out_16 = 1'b0;
  assign out_17 = 1'b0;
  assign out_18 = 4'b0000;

  // Notes on the sheet:
  //   Reg2
  //   EX
  //   Imm
  //   SET
  //   SSET
  //   RegWr
  //   ALUSrc
  //   ALUop
  //   MemToReg
  //   MemRd
  //   MemWr
  //   Branch
  //   J
  //   JR
  //   R7
  //   pc next
  //   Reg1
  //   Reg3
endmodule

module SSET (
  output out_1,
  output out_2,
  output out_3,
  output out_4,
  output out_5,
  output out_6,
  output out_7,
  output out_8,
  output out_9,
  output [4:0] out_10,
  output out_11,
  output out_12,
  output out_13,
  output out_14,
  output out_15,
  output out_16,
  output out_17,
  output [3:0] out_18
);


  assign out_1 = 1'b1;
  assign out_2 = 1'b0;
  assign out_3 = 1'b0;
  assign out_4 = 1'b1;
  assign out_5 = 1'b1;
  assign out_6 = 1'b0;
  assign out_7 = 1'b1;
  assign out_8 = 1'b1;
  assign out_9 = 1'b0;
  assign out_10 = 5'b11001;
  assign out_11 = 1'b0;
  assign out_12 = 1'b0;
  assign out_13 = 1'b0;
  assign out_14 = 1'b0;
  assign out_15 = 1'b0;
  assign out_16 = 1'b0;
  assign out_17 = 1'b0;
  assign out_18 = 4'b0000;

  // Notes on the sheet:
  //   Reg2
  //   EX
  //   Imm
  //   SET
  //   SSET
  //   RegWr
  //   ALUSrc
  //   ALUop
  //   MemToReg
  //   MemRd
  //   MemWr
  //   Branch
  //   J
  //   JR
  //   R7
  //   pc next
  //   Reg1
  //   Reg3
endmodule

module J (
  output out_1,
  output out_2,
  output out_3,
  output out_4,
  output out_5,
  output out_6,
  output out_7,
  output out_8,
  output out_9,
  output [4:0] out_10,
  output out_11,
  output out_12,
  output out_13,
  output out_14,
  output out_15,
  output out_16,
  output out_17,
  output [3:0] out_18
);


  assign out_1 = 1'b0;
  assign out_2 = 1'b0;
  assign out_3 = 1'b0;
  assign out_4 = 1'b0;
  assign out_5 = 1'b0;
  assign out_6 = 1'b0;
  assign out_7 = 1'b0;
  assign out_8 = 1'b0;
  assign out_9 = 1'b0;
  assign out_10 = 5'b11010;
  assign out_11 = 1'b0;
  assign out_12 = 1'b0;
  assign out_13 = 1'b0;
  assign out_14 = 1'b0;
  assign out_15 = 1'b1;
  assign out_16 = 1'b0;
  assign out_17 = 1'b0;
  assign out_18 = 4'b1000;

  // Notes on the sheet:
  //   Reg2
  //   EX
  //   Imm
  //   SET
  //   SSET
  //   RegWr
  //   ALUSrc
  //   ALUop
  //   MemToReg
  //   MemRd
  //   MemWr
  //   Branch
  //   J
  //   JR
  //   R7
  //   pc next
  //   Reg1
  //   Reg3
endmodule

module JAL (
  output out_1,
  output out_2,
  output out_3,
  output out_4,
  output out_5,
  output out_6,
  output out_7,
  output out_8,
  output out_9,
  output [4:0] out_10,
  output out_11,
  output out_12,
  output out_13,
  output out_14,
  output out_15,
  output out_16,
  output out_17,
  output [3:0] out_18
);


  assign out_1 = 1'b0;
  assign out_2 = 1'b1;
  assign out_3 = 1'b1;
  assign out_4 = 1'b0;
  assign out_5 = 1'b0;
  assign out_6 = 1'b0;
  assign out_7 = 1'b0;
  assign out_8 = 1'b1;
  assign out_9 = 1'b0;
  assign out_10 = 5'b11011;
  assign out_11 = 1'b0;
  assign out_12 = 1'b0;
  assign out_13 = 1'b0;
  assign out_14 = 1'b0;
  assign out_15 = 1'b1;
  assign out_16 = 1'b0;
  assign out_17 = 1'b1;
  assign out_18 = 4'b1000;

  // Notes on the sheet:
  //   Reg2
  //   EX
  //   Imm
  //   SET
  //   SSET
  //   RegWr
  //   ALUSrc
  //   ALUop
  //   MemToReg
  //   MemRd
  //   MemWr
  //   Branch
  //   J
  //   JR
  //   R7
  //   pc next
  //   Reg1
  //   Reg3
endmodule

module IF_ID_register (
  input  [19:0] PC,
  input  [15:0] Inst,
  input  Enable,
  input  clear,
  input  clk,
  output [19:0] PC_2,
  output [15:0] Inst_2
);

  Register #(.width(20)) register_1 (.D(PC), .en(Enable), .Q(PC_2), .clk(clk), .clr(clear));
  Register #(.width(16)) register_2 (.D(Inst), .en(Enable), .Q(Inst_2), .clk(clk), .clr(clear));
endmodule

module comparator (
  input  [31:0] in_1,
  input  [31:0] in_2,
  output Bne,
  output Beq,
  output BNEZ,
  output BEQZ,
  output BGTZ,
  output BLTZ,
  output BGEZ,
  output BLEZ
);

  Comparator #(.width(32)) comparator_1 (.a(in_1), .b(in_2), .eq(Beq));  // open: gt, lt
  Comparator #(.width(32)) comparator_2 (.a(in_2), .b({32{1'b0}}), .gt(BGTZ), .eq(BEQZ), .lt(BLTZ));
  not not_1 (BNEZ, BEQZ);
  not not_2 (Bne, Beq);
  not not_3 (BGEZ, BLTZ);
  not not_4 (BLEZ, BGTZ);

  // Other names for the same wires on the sheet: A[31:0] = in_1; B[31:0] = in_2
endmodule

module ID_EX (
  input  Imm,
  input  [3:0] pc_next,
  input  SET,
  input  SSET,
  input  R7,
  input  MemToReg,
  input  RegWr,
  input  MemRd,
  input  MemWr,
  input  Reg3,
  input  ALUSrc,
  input  [4:0] ALUop,
  input  [7:0] Imm8,
  input  [31:0] PC_1,
  input  [31:0] Imm_SignEX,
  input  [31:0] BusA,
  input  [31:0] BusB,
  input  [2:0] Rd,
  input  [2:0] Reg7,
  input  [2:0] Rs,
  input  [2:0] Rt,
  input  [1:0] Func,
  input  [4:0] Imm5,
  input  [10:0] Imm11,
  input  [4:0] opcode,
  input  J,
  input  JR,
  input  clear,
  input  CLK,
  output Imm_2,
  output [3:0] pc_next_2,
  output SET_2,
  output SSET_2,
  output R7_2,
  output MemToReg_2,
  output RegWr_2,
  output MemRd_2,
  output MemWr_2,
  output Reg3_2,
  output ALUSrc_2,
  output [4:0] ALUop_2,
  output [7:0] Imm8_2,
  output [31:0] PC_1_2,
  output [31:0] Imm_SingEx,
  output [31:0] BusA_2,
  output [31:0] BusB_2,
  output [2:0] Rd_2,
  output [2:0] Reg7_2,
  output [2:0] Rs_2,
  output [2:0] Rt_2,
  output [1:0] Func_2,
  output [4:0] Imm5_2,
  output [10:0] Imm11_2,
  output [4:0] opcode_2,
  output J_2,
  output JR_2
);

  Register #(.width(1)) register_1 (.D(Imm), .en(1'b1), .Q(Imm_2), .clk(CLK), .clr(clear));
  Register #(.width(4)) register_2 (.D(pc_next), .en(1'b1), .Q(pc_next_2), .clk(CLK), .clr(clear));
  Register #(.width(1)) register_3 (.D(SET), .en(1'b1), .Q(SET_2), .clk(CLK), .clr(clear));
  Register #(.width(1)) register_4 (.D(SSET), .en(1'b1), .Q(SSET_2), .clk(CLK), .clr(clear));
  Register #(.width(1)) register_5 (.D(R7), .en(1'b1), .Q(R7_2), .clk(CLK), .clr(clear));
  Register #(.width(1)) register_6 (.D(MemToReg), .en(1'b1), .Q(MemToReg_2), .clk(CLK), .clr(clear));
  Register #(.width(1)) register_7 (.D(RegWr), .en(1'b1), .Q(RegWr_2), .clk(CLK), .clr(clear));
  Register #(.width(1)) register_8 (.D(MemRd), .en(1'b1), .Q(MemRd_2), .clk(CLK), .clr(clear));
  Register #(.width(1)) register_9 (.D(MemWr), .en(1'b1), .Q(MemWr_2), .clk(CLK), .clr(clear));
  Register #(.width(1)) register_10 (.D(Reg3), .en(1'b1), .Q(Reg3_2), .clk(CLK), .clr(clear));
  Register #(.width(1)) register_11 (.D(ALUSrc), .en(1'b1), .Q(ALUSrc_2), .clk(CLK), .clr(clear));
  Register #(.width(5)) register_12 (.D(ALUop), .en(1'b1), .Q(ALUop_2), .clk(CLK), .clr(clear));
  Register register_13 (.D(Imm8), .en(1'b1), .Q(Imm8_2), .clk(CLK), .clr(clear));
  Register #(.width(32)) register_14 (.D(PC_1), .en(1'b1), .Q(PC_1_2), .clk(CLK), .clr(clear));
  Register #(.width(32)) register_15 (.D(Imm_SignEX), .en(1'b1), .Q(Imm_SingEx), .clk(CLK), .clr(clear));
  Register #(.width(32)) register_16 (.D(BusA), .en(1'b1), .Q(BusA_2), .clk(CLK), .clr(clear));
  Register #(.width(32)) register_17 (.D(BusB), .en(1'b1), .Q(BusB_2), .clk(CLK), .clr(clear));
  Register #(.width(3)) register_18 (.D(Rd), .en(1'b1), .Q(Rd_2), .clk(CLK), .clr(clear));
  Register #(.width(3)) register_19 (.D(Reg7), .en(1'b1), .Q(Reg7_2), .clk(CLK), .clr(clear));
  Register #(.width(3)) register_20 (.D(Rs), .en(1'b1), .Q(Rs_2), .clk(CLK), .clr(clear));
  Register #(.width(3)) register_21 (.D(Rt), .en(1'b1), .Q(Rt_2), .clk(CLK), .clr(clear));
  Register #(.width(2)) register_22 (.D(Func), .en(1'b1), .Q(Func_2), .clk(CLK), .clr(clear));
  Register #(.width(5)) register_23 (.D(Imm5), .en(1'b1), .Q(Imm5_2), .clk(CLK), .clr(clear));
  Register #(.width(11)) register_24 (.D(Imm11), .en(1'b1), .Q(Imm11_2), .clk(CLK), .clr(clear));
  Register #(.width(5)) register_25 (.D(opcode), .en(1'b1), .Q(opcode_2), .clk(CLK), .clr(clear));
  Register #(.width(1)) register_26 (.D(J), .en(1'b1), .Q(J_2), .clk(CLK), .clr(clear));
  Register #(.width(1)) register_27 (.D(JR), .en(1'b1), .Q(JR_2), .clk(CLK), .clr(clear));
endmodule

module EX_Mem (
  input  Imm,
  input  [3:0] pc_next,
  input  SET,
  input  SSET,
  input  MemToReg,
  input  RegWr,
  input  R7,
  input  MemRd,
  input  MemWr,
  input  [31:0] Result,
  input  [31:0] BusB,
  input  [2:0] Rd,
  input  [7:0] Imm8,
  input  [31:0] PC_1,
  input  [31:0] SSETvalue,
  input  [4:0] Imm5,
  input  [10:0] Imm11,
  input  [4:0] opcode,
  input  J,
  input  JR,
  input  clear,
  input  CLK,
  output Imm_2,
  output [3:0] pc_next_2,
  output SET_2,
  output SSET_2,
  output MemToReg_2,
  output RegWr_2,
  output R7_2,
  output MemRd_2,
  output MemWr_2,
  output [31:0] Result_2,
  output [31:0] BusB_2,
  output [2:0] Rd_2,
  output [7:0] Imm8_2,
  output [31:0] PC_1_2,
  output [31:0] SSETvalue_2,
  output [4:0] Imm5_2,
  output [10:0] Imm11_2,
  output [4:0] opcode_2,
  output J_2,
  output JR_2
);

  Register #(.width(1)) register_1 (.D(Imm), .en(1'b1), .Q(Imm_2), .clk(CLK), .clr(clear));
  Register #(.width(4)) register_2 (.D(pc_next), .en(1'b1), .Q(pc_next_2), .clk(CLK), .clr(clear));
  Register #(.width(1)) register_3 (.D(SET), .en(1'b1), .Q(SET_2), .clk(CLK), .clr(clear));
  Register #(.width(1)) register_4 (.D(SSET), .en(1'b1), .Q(SSET_2), .clk(CLK), .clr(clear));
  Register #(.width(1)) register_5 (.D(MemToReg), .en(1'b1), .Q(MemToReg_2), .clk(CLK), .clr(clear));
  Register #(.width(1)) register_6 (.D(RegWr), .en(1'b1), .Q(RegWr_2), .clk(CLK), .clr(clear));
  Register #(.width(1)) register_7 (.D(R7), .en(1'b1), .Q(R7_2), .clk(CLK), .clr(clear));
  Register #(.width(1)) register_8 (.D(MemRd), .en(1'b1), .Q(MemRd_2), .clk(CLK), .clr(clear));
  Register #(.width(1)) register_9 (.D(MemWr), .en(1'b1), .Q(MemWr_2), .clk(CLK), .clr(clear));
  Register #(.width(32)) register_10 (.D(Result), .en(1'b1), .Q(Result_2), .clk(CLK), .clr(clear));
  Register #(.width(32)) register_11 (.D(BusB), .en(1'b1), .Q(BusB_2), .clk(CLK), .clr(clear));
  Register #(.width(3)) register_12 (.D(Rd), .en(1'b1), .Q(Rd_2), .clk(CLK), .clr(clear));
  Register register_13 (.D(Imm8), .en(1'b1), .Q(Imm8_2), .clk(CLK), .clr(clear));
  Register #(.width(32)) register_14 (.D(PC_1), .en(1'b1), .Q(PC_1_2), .clk(CLK), .clr(clear));
  Register #(.width(32)) register_15 (.D(SSETvalue), .en(1'b1), .Q(SSETvalue_2), .clk(CLK), .clr(clear));
  Register #(.width(5)) register_16 (.D(Imm5), .en(1'b1), .Q(Imm5_2), .clk(CLK), .clr(clear));
  Register #(.width(11)) register_17 (.D(Imm11), .en(1'b1), .Q(Imm11_2), .clk(CLK), .clr(clear));
  Register #(.width(5)) register_18 (.D(opcode), .en(1'b1), .Q(opcode_2), .clk(CLK), .clr(clear));
  Register #(.width(1)) register_19 (.D(J), .en(1'b1), .Q(J_2), .clk(CLK), .clr(clear));
  Register #(.width(1)) register_20 (.D(JR), .en(1'b1), .Q(JR_2), .clk(CLK), .clr(clear));
endmodule

module Mem_WB (
  input  Imm,
  input  [3:0] pc_next,
  input  SET,
  input  SSET,
  input  MemToReg,
  input  RegWr,
  input  R7,
  input  [2:0] Rd,
  input  [31:0] Result,
  input  [31:0] DataRd,
  input  [7:0] Imm8,
  input  [31:0] PC_1,
  input  [31:0] SSETvalue,
  input  [4:0] Imm5,
  input  [10:0] Imm11,
  input  [4:0] opcode,
  input  J,
  input  JR,
  input  MemRd,
  input  clear,
  input  CLK,
  output Imm_2,
  output [3:0] pc_next_2,
  output SET_2,
  output SSET_2,
  output MemToReg_2,
  output RegWr_2,
  output R7_2,
  output [2:0] Rd_2,
  output [31:0] Result_2,
  output [31:0] DataRd_2,
  output [7:0] Imm8_2,
  output [31:0] PC_1_2,
  output [31:0] SSETvalue_2,
  output [4:0] Imm5_2,
  output [10:0] Imm11_2,
  output [4:0] opcode_2,
  output J_2,
  output JR_2,
  output MemRd_2
);

  Register #(.width(1)) register_1 (.D(Imm), .en(1'b1), .Q(Imm_2), .clk(CLK), .clr(clear));
  Register #(.width(4)) register_2 (.D(pc_next), .en(1'b1), .Q(pc_next_2), .clk(CLK), .clr(clear));
  Register #(.width(1)) register_3 (.D(SET), .en(1'b1), .Q(SET_2), .clk(CLK), .clr(clear));
  Register #(.width(1)) register_4 (.D(SSET), .en(1'b1), .Q(SSET_2), .clk(CLK), .clr(clear));
  Register #(.width(1)) register_5 (.D(MemToReg), .en(1'b1), .Q(MemToReg_2), .clk(CLK), .clr(clear));
  Register #(.width(1)) register_6 (.D(RegWr), .en(1'b1), .Q(RegWr_2), .clk(CLK), .clr(clear));
  Register #(.width(1)) register_7 (.D(R7), .en(1'b1), .Q(R7_2), .clk(CLK), .clr(clear));
  Register #(.width(3)) register_8 (.D(Rd), .en(1'b1), .Q(Rd_2), .clk(CLK), .clr(clear));
  Register #(.width(32)) register_9 (.D(Result), .en(1'b1), .Q(Result_2), .clk(CLK), .clr(clear));
  Register #(.width(32)) register_10 (.D(DataRd), .en(1'b1), .Q(DataRd_2), .clk(CLK), .clr(clear));
  Register register_11 (.D(Imm8), .en(1'b1), .Q(Imm8_2), .clk(CLK), .clr(clear));
  Register #(.width(32)) register_12 (.D(PC_1), .en(1'b1), .Q(PC_1_2), .clk(CLK), .clr(clear));
  Register #(.width(32)) register_13 (.D(SSETvalue), .en(1'b1), .Q(SSETvalue_2), .clk(CLK), .clr(clear));
  Register #(.width(5)) register_14 (.D(Imm5), .en(1'b1), .Q(Imm5_2), .clk(CLK), .clr(clear));
  Register #(.width(11)) register_15 (.D(Imm11), .en(1'b1), .Q(Imm11_2), .clk(CLK), .clr(clear));
  Register #(.width(5)) register_16 (.D(opcode), .en(1'b1), .Q(opcode_2), .clk(CLK), .clr(clear));
  Register #(.width(1)) register_17 (.D(J), .en(1'b1), .Q(J_2), .clk(CLK), .clr(clear));
  Register #(.width(1)) register_18 (.D(JR), .en(1'b1), .Q(JR_2), .clk(CLK), .clr(clear));
  Register #(.width(1)) register_19 (.D(MemRd), .en(1'b1), .Q(MemRd_2), .clk(CLK), .clr(clear));
endmodule

module Forward_Unit (
  input  [2:0] ID_EX_Rs,
  input  [2:0] ID_EX_Rt,
  input  [2:0] ID_EX_Rd,
  input  [2:0] EX_Mem_Rd,
  input  [2:0] Mem_WB_Rd,
  input  ID_Ex_SSET,
  input  Ex_Mem_RegWr,
  input  Mem_WB_RegWr,
  input  [4:0] opcode_id_ex,
  input  Ex_Mem_sset,
  input  Ex_Mem_set,
  input  Ex_Mem_j,
  input  Ex_Mem_jr,
  input  Mem_WB_sset,
  input  Mem_WB_set,
  input  Mem_WB_jr,
  input  Mem_WB_j,
  input  Mem_WB_mem_read,
  input  [4:0] opcode_ex_mem,
  input  [4:0] opcode_mem_wb,
  input  ex_mem_mem_read,
  output [3:0] FWD_B,
  output [3:0] FWD_A
);

  wire and_1_out, and_2_out, and_3_out, and_4_out, and_5_out, and_6_out, and_7_out, and_8_out, and_9_out,
       and_10_out, and_11_out, and_12_out, and_13_out, and_14_out, and_15_out, and_16_out, and_17_out,
       and_18_out, and_19_out, and_20_out, and_21_out, and_22_out, and_23_out, and_24_out, and_25_out,
       and_26_out, and_27_out, and_28_out, and_29_out, and_30_out, and_31_out, and_32_out, and_33_out,
       and_34_out, and_35_out, and_36_out, and_37_out, and_38_out, and_39_out, and_40_out, and_41_out,
       and_42_out, and_43_out, and_44_out, and_45_out, comparator_1_eq, comparator_2_eq, comparator_3_eq,
       comparator_4_eq, comparator_5_eq, comparator_6_eq, comparator_7_eq, comparator_8_eq, comparator_9_eq,
       comparator_10_eq, comparator_11_eq, comparator_12_eq, comparator_13_eq, comparator_14_eq,
       comparator_15_eq, comparator_16_eq, comparator_17_eq, comparator_18_eq, comparator_19_eq,
       comparator_20_eq, comparator_21_eq, comparator_22_eq, comparator_23_eq, comparator_24_eq,
       comparator_25_eq, comparator_26_eq, comparator_27_eq, i_type, i_type_ex_mem, i_type_mem_wb, not_1_out,
       not_2_out, not_3_out, not_4_out, not_5_out, not_6_out, not_7_out, not_8_out, not_9_out, not_10_out,
       not_11_out, not_12_out, not_13_out, not_14_out, or_4_out, or_5_out, or_6_out, or_7_out, or_8_out,
       or_9_out, or_10_out, or_11_out, or_12_out, or_13_out, or_14_out, or_15_out, or_16_out, r_i,
       r_i_ex_mem, r_i_mem_wb, r_type, r_type_ex_mem, r_type_mem_wb;
  wire [3:0] multiplexer_1_out, multiplexer_2_out, multiplexer_3_out, multiplexer_4_out, multiplexer_5_out,
       multiplexer_6_out, multiplexer_7_out, multiplexer_8_out, multiplexer_10_out, multiplexer_11_out,
       multiplexer_12_out, multiplexer_13_out, multiplexer_14_out, multiplexer_15_out, multiplexer_16_out,
       multiplexer_17_out;

  r_i_type r_i_type_1 (.opcode(opcode_id_ex), .i_type(i_type), .r_type(r_type));
  or or_1 (r_i, i_type, r_type);
  r_i_type r_i_type_2 (.opcode(opcode_ex_mem), .i_type(i_type_ex_mem), .r_type(r_type_ex_mem));
  r_i_type r_i_type_3 (.opcode(opcode_mem_wb), .i_type(i_type_mem_wb), .r_type(r_type_mem_wb));
  or or_2 (r_i_ex_mem, i_type_ex_mem, r_type_ex_mem);
  or or_3 (r_i_mem_wb, i_type_mem_wb, r_type_mem_wb);
  Comparator #(.width(3)) comparator_1 (.a(ID_EX_Rs), .b(Mem_WB_Rd), .eq(comparator_1_eq));  // open: gt, lt
  Comparator #(.width(3)) comparator_2 (.a(ID_EX_Rd), .b(Mem_WB_Rd), .eq(comparator_2_eq));  // open: gt, lt
  Comparator #(.width(3)) comparator_3 (.a(ID_EX_Rs), .b(Mem_WB_Rd), .eq(comparator_3_eq));  // open: gt, lt
  Comparator #(.width(3)) comparator_4 (.a(ID_EX_Rd), .b(Mem_WB_Rd), .eq(comparator_4_eq));  // open: gt, lt
  Comparator #(.width(3)) comparator_5 (.a(ID_EX_Rs), .b(Mem_WB_Rd), .eq(comparator_5_eq));  // open: gt, lt
  Comparator #(.width(3)) comparator_6 (.a(ID_EX_Rd), .b(Mem_WB_Rd), .eq(comparator_6_eq));  // open: gt, lt
  Comparator #(.width(3)) comparator_7 (.a(ID_EX_Rs), .b(Mem_WB_Rd), .eq(comparator_7_eq));  // open: gt, lt
  Comparator #(.width(3)) comparator_8 (.a(ID_EX_Rd), .b(Mem_WB_Rd), .eq(comparator_8_eq));  // open: gt, lt
  Comparator #(.width(3)) comparator_9 (.a(ID_EX_Rs), .b(Mem_WB_Rd), .eq(comparator_9_eq));  // open: gt, lt
  Comparator #(.width(3)) comparator_10 (.a(ID_EX_Rd), .b(Mem_WB_Rd), .eq(comparator_10_eq));  // open: gt, lt
  Comparator #(.width(3)) comparator_11 (.a(ID_EX_Rs), .b(EX_Mem_Rd), .eq(comparator_11_eq));  // open: gt, lt
  Comparator #(.width(3)) comparator_12 (.a(ID_EX_Rd), .b(EX_Mem_Rd), .eq(comparator_12_eq));  // open: gt, lt
  Comparator #(.width(3)) comparator_13 (.a(ID_EX_Rs), .b(EX_Mem_Rd), .eq(comparator_13_eq));  // open: gt, lt
  Comparator #(.width(3)) comparator_14 (.a(ID_EX_Rd), .b(EX_Mem_Rd), .eq(comparator_14_eq));  // open: gt, lt
  Comparator #(.width(3)) comparator_15 (.a(ID_EX_Rs), .b(EX_Mem_Rd), .eq(comparator_15_eq));  // open: gt, lt
  Comparator #(.width(3)) comparator_16 (.a(ID_EX_Rd), .b(EX_Mem_Rd), .eq(comparator_16_eq));  // open: gt, lt
  Comparator #(.width(3)) comparator_17 (.a(ID_EX_Rs), .b(EX_Mem_Rd), .eq(comparator_17_eq));  // open: gt, lt
  Comparator #(.width(3)) comparator_18 (.a(ID_EX_Rd), .b(EX_Mem_Rd), .eq(comparator_18_eq));  // open: gt, lt
  and and_1 (and_1_out, r_i, comparator_11_eq);
  and and_2 (and_2_out, comparator_12_eq, ID_Ex_SSET);
  and and_3 (and_3_out, r_i, comparator_13_eq);
  and and_4 (and_4_out, comparator_14_eq, ID_Ex_SSET);
  and and_5 (and_5_out, r_i, comparator_15_eq);
  and and_6 (and_6_out, comparator_16_eq, ID_Ex_SSET);
  and and_7 (and_7_out, r_i, comparator_17_eq);
  and and_8 (and_8_out, comparator_18_eq, ID_Ex_SSET);
  and and_9 (and_9_out, r_i, comparator_1_eq);
  and and_10 (and_10_out, comparator_2_eq, ID_Ex_SSET);
  and and_11 (and_11_out, r_i, comparator_3_eq);
  and and_12 (and_12_out, comparator_4_eq, ID_Ex_SSET);
  and and_13 (and_13_out, r_i, comparator_5_eq);
  and and_14 (and_14_out, comparator_6_eq, ID_Ex_SSET);
  and and_15 (and_15_out, r_i, comparator_7_eq);
  and and_16 (and_16_out, comparator_8_eq, ID_Ex_SSET);
  and and_17 (and_17_out, r_i, comparator_9_eq);
  and and_18 (and_18_out, comparator_10_eq, ID_Ex_SSET);
  or or_4 (or_4_out, and_1_out, and_2_out);
  or or_5 (or_5_out, and_3_out, and_4_out);
  or or_6 (or_6_out, and_5_out, and_6_out);
  or or_7 (or_7_out, and_7_out, and_8_out);
  or or_8 (or_8_out, and_9_out, and_10_out);
  or or_9 (or_9_out, and_11_out, and_12_out);
  or or_10 (or_10_out, and_13_out, and_14_out);
  or or_11 (or_11_out, and_15_out, and_16_out);
  or or_12 (or_12_out, and_17_out, and_18_out);
  not not_1 (not_1_out, ex_mem_mem_read);
  or or_13 (or_13_out, Ex_Mem_jr, Ex_Mem_j);
  or or_14 (or_14_out, Mem_WB_jr, Mem_WB_j);
  and and_19 (and_19_out, not_1_out, Ex_Mem_RegWr, r_i_ex_mem, or_4_out);
  not not_2 (not_2_out, Ex_Mem_RegWr);
  not not_3 (not_3_out, Mem_WB_mem_read);
  not not_4 (not_4_out, Ex_Mem_RegWr);
  not not_5 (not_5_out, Ex_Mem_RegWr);
  not not_6 (not_6_out, Ex_Mem_RegWr);
  not not_7 (not_7_out, Ex_Mem_RegWr);
  and and_20 (and_20_out, or_5_out, Ex_Mem_RegWr, Ex_Mem_sset);
  and and_21 (and_21_out, or_6_out, Ex_Mem_RegWr, Ex_Mem_set);
  and and_22 (and_22_out, or_7_out, Ex_Mem_RegWr, or_13_out);
  and and_23 (and_23_out, not_2_out, Mem_WB_RegWr, r_i_mem_wb, not_3_out, or_8_out);
  and and_24 (and_24_out, not_4_out, Mem_WB_RegWr, or_9_out, Mem_WB_mem_read);
  and and_25 (and_25_out, not_5_out, or_10_out, Mem_WB_sset);
  and and_26 (and_26_out, not_6_out, or_11_out, Mem_WB_set);
  and and_27 (and_27_out, not_7_out, Mem_WB_RegWr, or_12_out, or_14_out);
  Multiplexer #(.width(4), .enable("false")) multiplexer_1 (
    .in0(4'b0000), .in1(4'b0001), .out(multiplexer_1_out), .sel(and_19_out));
  Multiplexer #(.width(4), .enable("false")) multiplexer_2 (
    .in0(multiplexer_1_out), .in1(4'b0010), .out(multiplexer_2_out), .sel(and_20_out));
  Multiplexer #(.width(4), .enable("false")) multiplexer_3 (
    .in0(multiplexer_2_out), .in1(4'b0011), .out(multiplexer_3_out), .sel(and_21_out));
  Multiplexer #(.width(4), .enable("false")) multiplexer_4 (
    .in0(multiplexer_3_out), .in1(4'b0100), .out(multiplexer_4_out), .sel(and_22_out));
  Multiplexer #(.width(4), .enable("false")) multiplexer_5 (
    .in0(multiplexer_4_out), .in1(4'b0101), .out(multiplexer_5_out), .sel(and_23_out));
  Multiplexer #(.width(4), .enable("false")) multiplexer_6 (
    .in0(multiplexer_5_out), .in1(4'b0110), .out(multiplexer_6_out), .sel(and_24_out));
  Multiplexer #(.width(4), .enable("false")) multiplexer_7 (
    .in0(multiplexer_6_out), .in1(4'b0111), .out(multiplexer_7_out), .sel(and_25_out));
  Multiplexer #(.width(4), .enable("false")) multiplexer_8 (
    .in0(multiplexer_7_out), .in1(4'b1000), .out(multiplexer_8_out), .sel(and_26_out));
  Multiplexer #(.width(4), .enable("false")) multiplexer_9 (
    .in0(multiplexer_8_out), .in1(4'b1001), .out(FWD_A), .sel(and_27_out));
  Comparator #(.width(3)) comparator_19 (.a(ID_EX_Rt), .b(Mem_WB_Rd), .eq(comparator_19_eq));  // open: gt, lt
  Comparator #(.width(3)) comparator_20 (.a(ID_EX_Rt), .b(Mem_WB_Rd), .eq(comparator_20_eq));  // open: gt, lt
  Comparator #(.width(3)) comparator_21 (.a(ID_EX_Rt), .b(Mem_WB_Rd), .eq(comparator_21_eq));  // open: gt, lt
  Comparator #(.width(3)) comparator_22 (.a(ID_EX_Rt), .b(Mem_WB_Rd), .eq(comparator_22_eq));  // open: gt, lt
  Comparator #(.width(3)) comparator_23 (.a(ID_EX_Rt), .b(EX_Mem_Rd), .eq(comparator_23_eq));  // open: gt, lt
  Comparator #(.width(3)) comparator_24 (.a(ID_EX_Rt), .b(EX_Mem_Rd), .eq(comparator_24_eq));  // open: gt, lt
  Comparator #(.width(3)) comparator_25 (.a(ID_EX_Rt), .b(EX_Mem_Rd), .eq(comparator_25_eq));  // open: gt, lt
  Comparator #(.width(3)) comparator_26 (.a(ID_EX_Rt), .b(EX_Mem_Rd), .eq(comparator_26_eq));  // open: gt, lt
  and and_28 (and_28_out, r_type, comparator_19_eq);
  and and_29 (and_29_out, r_type, comparator_20_eq);
  and and_30 (and_30_out, r_type, comparator_21_eq);
  and and_31 (and_31_out, r_type, comparator_22_eq);
  Comparator #(.width(3)) comparator_27 (.a(ID_EX_Rt), .b(Mem_WB_Rd), .eq(comparator_27_eq));  // open: gt, lt
  and and_32 (and_32_out, r_type, comparator_23_eq);
  and and_33 (and_33_out, r_type, comparator_24_eq);
  and and_34 (and_34_out, r_type, comparator_25_eq);
  and and_35 (and_35_out, r_type, comparator_26_eq);
  and and_36 (and_36_out, r_type, comparator_27_eq);
  or or_15 (or_15_out, Ex_Mem_jr, Ex_Mem_j);
  not not_8 (not_8_out, ex_mem_mem_read);
  not not_9 (not_9_out, Ex_Mem_RegWr);
  not not_10 (not_10_out, Mem_WB_mem_read);
  not not_11 (not_11_out, Ex_Mem_RegWr);
  not not_12 (not_12_out, Ex_Mem_RegWr);
  not not_13 (not_13_out, Ex_Mem_RegWr);
  not not_14 (not_14_out, Ex_Mem_RegWr);
  or or_16 (or_16_out, Mem_WB_jr, Mem_WB_j);
  and and_37 (and_37_out, not_8_out, Ex_Mem_RegWr, and_32_out);
  and and_38 (and_38_out, and_33_out, Ex_Mem_RegWr, Ex_Mem_sset);
  and and_39 (and_39_out, and_34_out, Ex_Mem_RegWr, Ex_Mem_set);
  and and_40 (and_40_out, and_35_out, Ex_Mem_RegWr, or_15_out);
  and and_41 (and_41_out, not_9_out, Mem_WB_RegWr, r_type_ex_mem, not_10_out, and_28_out);
  and and_42 (and_42_out, not_11_out, Mem_WB_RegWr, and_29_out, Mem_WB_mem_read);
  and and_43 (and_43_out, not_12_out, and_30_out, Mem_WB_sset);
  and and_44 (and_44_out, not_13_out, and_31_out, Mem_WB_set);
  and and_45 (and_45_out, not_14_out, Mem_WB_RegWr, and_36_out, or_16_out);
  Multiplexer #(.width(4), .enable("false")) multiplexer_10 (
    .in0(4'b0000), .in1(4'b0001), .out(multiplexer_10_out), .sel(and_37_out));
  Multiplexer #(.width(4), .enable("false")) multiplexer_11 (
    .in0(multiplexer_10_out), .in1(4'b0010), .out(multiplexer_11_out), .sel(and_38_out));
  Multiplexer #(.width(4), .enable("false")) multiplexer_12 (
    .in0(multiplexer_11_out), .in1(4'b0011), .out(multiplexer_12_out), .sel(and_39_out));
  Multiplexer #(.width(4), .enable("false")) multiplexer_13 (
    .in0(multiplexer_12_out), .in1(4'b0100), .out(multiplexer_13_out), .sel(and_40_out));
  Multiplexer #(.width(4), .enable("false")) multiplexer_14 (
    .in0(multiplexer_13_out), .in1(4'b0101), .out(multiplexer_14_out), .sel(and_41_out));
  Multiplexer #(.width(4), .enable("false")) multiplexer_15 (
    .in0(multiplexer_14_out), .in1(4'b0110), .out(multiplexer_15_out), .sel(and_42_out));
  Multiplexer #(.width(4), .enable("false")) multiplexer_16 (
    .in0(multiplexer_15_out), .in1(4'b0111), .out(multiplexer_16_out), .sel(and_43_out));
  Multiplexer #(.width(4), .enable("false")) multiplexer_17 (
    .in0(multiplexer_16_out), .in1(4'b1000), .out(multiplexer_17_out), .sel(and_44_out));
  Multiplexer #(.width(4), .enable("false")) multiplexer_18 (
    .in0(multiplexer_17_out), .in1(4'b1001), .out(FWD_B), .sel(and_45_out));

  // Other names for the same wires on the sheet: ex_mem__mem_read = ex_mem_mem_read; Ex_Mem_jal = Ex_Mem_j;
  //   Ex_Mem_jalr = Ex_Mem_jr; Mem_WB_jal = Mem_WB_j; Mem_WB_jalr = Mem_WB_jr

  // Notes on the sheet:
  //   from alu
  //   from sset
  //   from set
  //   from jal/jalr
  //   from alu
  //   from mem
  //   from sset
  //   from set
  //   from jal/jalr
  //   from alu
  //   from sset
  //   from set
  //   from jal/jalr
  //   from alu
  //   from mem
  //   from sset
  //   from set
  //   from jal/jalr
endmodule

module Branch_Fwd_unit (
  input  JR,
  input  branch,
  input  ex_mem_mem_read,
  input  [2:0] IF_ID_Rs,
  input  Ex_Mem_RegWr,
  input  [2:0] Ex_Mem_Rd,
  input  Ex_Mem_SSET,
  input  Ex_Mem_set,
  input  Ex_Mem____j,
  input  Ex_Mem____jr,
  input  [4:0] opcode_ex_mem,
  input  [2:0] IF_ID_Rd,
  input  [3:0] next_pc,
  output [2:0] FWD_C,
  output [2:0] FWD_D
);

  wire and_1_out, and_2_out, and_3_out, and_4_out, and_5_out, and_6_out, and_7_out, and_8_out, and_9_out,
       and_10_out, comparator_1_eq, comparator_2_eq, comparator_3_eq, comparator_4_eq, i_type_ex_mem,
       not_1_out, not_2_out, or_2_out, or_3_out, or_4_out, or_5_out, r_i_ex_mem, r_type_ex_mem;
  wire [2:0] multiplexer_1_out, multiplexer_2_out, multiplexer_3_out, multiplexer_5_out, multiplexer_6_out,
       multiplexer_7_out;

  r_i_type r_i_type_1 (.opcode(opcode_ex_mem), .i_type(i_type_ex_mem), .r_type(r_type_ex_mem));
  or or_1 (r_i_ex_mem, i_type_ex_mem, r_type_ex_mem);
  Comparator #(.width(4)) comparator_1 (.a(next_pc), .b(4'b0000), .eq(comparator_1_eq));  // open: gt, lt
  Comparator #(.width(4)) comparator_2 (.a(next_pc), .b(4'b0001), .eq(comparator_2_eq));  // open: gt, lt
  or or_2 (or_2_out, comparator_1_eq, comparator_2_eq);
  Comparator #(.width(3)) comparator_3 (.a(IF_ID_Rs), .b(Ex_Mem_Rd), .eq(comparator_3_eq));  // open: gt, lt
  Comparator #(.width(3)) comparator_4 (.a(IF_ID_Rd), .b(Ex_Mem_Rd), .eq(comparator_4_eq));  // open: gt, lt
  or or_3 (or_3_out, JR, branch);
  and and_1 (and_1_out, or_3_out, and_2_out);
  and and_2 (and_2_out, comparator_3_eq, or_2_out);
  or or_4 (or_4_out, Ex_Mem____j, Ex_Mem____jr);
  or or_5 (or_5_out, Ex_Mem____j, Ex_Mem____jr);
  not not_1 (not_1_out, ex_mem_mem_read);
  and and_3 (and_3_out, not_1_out, Ex_Mem_RegWr, and_1_out, r_i_ex_mem);
  and and_4 (and_4_out, and_1_out, Ex_Mem_RegWr, Ex_Mem_SSET);
  and and_5 (and_5_out, and_1_out, Ex_Mem_RegWr, Ex_Mem_set);
  and and_6 (and_6_out, and_1_out, Ex_Mem_RegWr, or_4_out);
  not not_2 (not_2_out, ex_mem_mem_read);
  and and_7 (and_7_out, not_2_out, comparator_4_eq, Ex_Mem_RegWr, r_i_ex_mem);
  and and_8 (and_8_out, comparator_4_eq, Ex_Mem_RegWr, Ex_Mem_SSET);
  and and_9 (and_9_out, comparator_4_eq, Ex_Mem_RegWr, Ex_Mem_set);
  and and_10 (and_10_out, comparator_4_eq, Ex_Mem_RegWr, or_5_out);
  Multiplexer #(.width(3), .enable("false")) multiplexer_1 (
    .in0(3'b000), .in1(3'b001), .out(multiplexer_1_out), .sel(and_3_out));
  Multiplexer #(.width(3), .enable("false")) multiplexer_2 (
    .in0(multiplexer_1_out), .in1(3'b010), .out(multiplexer_2_out), .sel(and_4_out));
  Multiplexer #(.width(3), .enable("false")) multiplexer_3 (
    .in0(multiplexer_2_out), .in1(3'b011), .out(multiplexer_3_out), .sel(and_5_out));
  Multiplexer #(.width(3), .enable("false")) multiplexer_4 (
    .in0(multiplexer_3_out), .in1(3'b100), .out(FWD_C), .sel(and_6_out));
  Multiplexer #(.width(3), .enable("false")) multiplexer_5 (
    .in0(3'b000), .in1(3'b001), .out(multiplexer_5_out), .sel(and_7_out));
  Multiplexer #(.width(3), .enable("false")) multiplexer_6 (
    .in0(multiplexer_5_out), .in1(3'b010), .out(multiplexer_6_out), .sel(and_8_out));
  Multiplexer #(.width(3), .enable("false")) multiplexer_7 (
    .in0(multiplexer_6_out), .in1(3'b011), .out(multiplexer_7_out), .sel(and_9_out));
  Multiplexer #(.width(3), .enable("false")) multiplexer_8 (
    .in0(multiplexer_7_out), .in1(3'b100), .out(FWD_D), .sel(and_10_out));

  // Other names for the same wires on the sheet: ex_mem__mem_read = ex_mem_mem_read; Ex_Mem_jal = Ex_Mem____j;
  //   Ex_Mem_jalr = Ex_Mem____jr

  // Notes on the sheet:
  //   from alu
  //   from sset
  //   from set
  //   from jal/jalr
  //   from alu
  //   from sset
  //   from set
  //   from jal/jalr
endmodule

module Hazard_detection_unit (
  input  ID_EX_MemRd,
  input  [2:0] IF_ID_Rs,
  input  [2:0] IF_ID_Rt,
  input  [2:0] ID_Ex_Rd,
  input  [2:0] IF_ID_Rd,
  input  IF_ID_SSET,
  input  [2:0] Ex_Mem_Rd,
  input  Ex_Mem_MemRD,
  input  Ex_Mem_RegWr,
  input  ID_EX_RegWr,
  input  Ex_Mem_SSET,
  input  ID_EX_SSET,
  input  [4:0] opcode_if_id,
  input  [3:0] next_pc,
  input  JR_jalr,
  input  branch_taken,
  output stall,
  output stall_2
);

  wire and_1_out, and_2_out, and_3_out, and_4_out, and_5_out, and_7_out, and_8_out, comparator_1_eq,
       comparator_2_eq, comparator_3_eq, comparator_4_eq, comparator_5_eq, comparator_6_eq, comparator_7_eq,
       comparator_8_eq, comparator_9_eq, i_type_if_id, or_2_out, or_3_out, or_4_out, or_5_out, or_6_out,
       or_7_out, r_i_if_id, r_type_if_id;

  r_i_type r_i_type_1 (.opcode(opcode_if_id), .i_type(i_type_if_id), .r_type(r_type_if_id));
  Comparator #(.width(4)) comparator_1 (.a(next_pc), .b(4'b0000), .eq(comparator_1_eq));  // open: gt, lt
  Comparator #(.width(4)) comparator_2 (.a(next_pc), .b(4'b0001), .eq(comparator_2_eq));  // open: gt, lt
  or or_1 (r_i_if_id, i_type_if_id, r_type_if_id);
  or or_2 (or_2_out, comparator_1_eq, comparator_2_eq);
  Comparator #(.width(3)) comparator_3 (.a(IF_ID_Rs), .b(ID_Ex_Rd), .eq(comparator_3_eq));  // open: gt, lt
  Comparator #(.width(3)) comparator_4 (.a(IF_ID_Rd), .b(ID_Ex_Rd), .eq(comparator_4_eq));  // open: gt, lt
  Comparator #(.width(3)) comparator_5 (.a(IF_ID_Rd), .b(Ex_Mem_Rd), .eq(comparator_5_eq));  // open: gt, lt
  Comparator #(.width(3)) comparator_6 (.a(IF_ID_Rs), .b(Ex_Mem_Rd), .eq(comparator_6_eq));  // open: gt, lt
  Comparator #(.width(3)) comparator_7 (.a(IF_ID_Rt), .b(ID_Ex_Rd), .eq(comparator_7_eq));  // open: gt, lt
  Comparator #(.width(3)) comparator_8 (.a(IF_ID_Rd), .b(ID_Ex_Rd), .eq(comparator_8_eq));  // open: gt, lt
  and and_1 (and_1_out, comparator_4_eq, or_2_out);
  Comparator #(.width(3)) comparator_9 (.a(IF_ID_Rs), .b(ID_Ex_Rd), .eq(comparator_9_eq));  // open: gt, lt
  and and_2 (and_2_out, or_2_out, comparator_5_eq);
  and and_3 (and_3_out, r_i_if_id, comparator_9_eq);
  and and_4 (and_4_out, r_type_if_id, comparator_7_eq);
  and and_5 (and_5_out, comparator_8_eq, IF_ID_SSET);
  or or_3 (or_3_out, and_2_out, comparator_6_eq);
  or or_4 (or_4_out, and_3_out, and_4_out, and_5_out);
  or or_5 (or_5_out, comparator_3_eq, and_1_out);
  and and_6 (stall, ID_EX_MemRd, or_4_out);
  and and_7 (and_7_out, or_3_out, Ex_Mem_MemRD);
  and and_8 (and_8_out, or_5_out, ID_EX_RegWr);
  or or_6 (or_6_out, and_8_out, and_7_out);
  or or_7 (or_7_out, JR_jalr, branch_taken);
  and and_9 (stall_2, or_6_out, or_7_out);
endmodule

module branch_taken (
  input  Branch,
  input  Bne,
  input  Beq,
  input  BNEZ,
  input  BEQZ,
  input  BGTZ,
  input  BLTZ,
  input  BGEZ,
  input  [3:0] PC_Next,
  input  BLEZ,
  output Branch_Taken
);

  wire and_1_out, and_2_out, and_3_out, and_4_out, and_5_out, and_6_out, and_7_out, and_8_out;

  and and_1 (and_1_out, Branch, Beq);
  and and_2 (and_2_out, Branch, Bne);
  and and_3 (and_3_out, Branch, BEQZ);
  and and_4 (and_4_out, Branch, BNEZ);
  and and_5 (and_5_out, Branch, BLTZ);
  and and_6 (and_6_out, Branch, BGEZ);
  and and_7 (and_7_out, Branch, BGTZ);
  and and_8 (and_8_out, Branch, BLEZ);
  Multiplexer #(.select(4), .enable("false")) multiplexer_1 (
    .in0(and_1_out), .in1(and_2_out), .in2(and_3_out), .in3(and_4_out), .in4(and_5_out), .in5(and_6_out),
    .in6(and_7_out), .in7(and_8_out), .out(Branch_Taken), .sel(PC_Next));  // open: in8, in9, in10, in11, in12, in13, in14, in15
endmodule

module r_i_type (
  input  [4:0] opcode,
  output i_type,
  output r_type
);

  wire comparator_1_eq, comparator_2_eq, comparator_3_eq, comparator_4_eq, comparator_5_eq, comparator_6_eq,
       comparator_7_eq, comparator_8_eq, comparator_9_eq, comparator_10_eq, comparator_11_eq,
       comparator_12_eq, comparator_13_eq, comparator_14_eq;

  Comparator #(.width(5)) comparator_1 (.a(opcode), .b(5'b10000), .eq(comparator_1_eq));  // open: gt, lt
  Comparator #(.width(5)) comparator_2 (.a(opcode), .b(5'b10001), .eq(comparator_2_eq));  // open: gt, lt
  Comparator #(.width(5)) comparator_3 (.a(opcode), .b(5'b00100), .eq(comparator_3_eq));  // open: gt, lt
  Comparator #(.width(5)) comparator_4 (.a(opcode), .b(5'b00101), .eq(comparator_4_eq));  // open: gt, lt
  Comparator #(.width(5)) comparator_5 (.a(opcode), .b(5'b00110), .eq(comparator_5_eq));  // open: gt, lt
  Comparator #(.width(5)) comparator_6 (.a(opcode), .b(5'b00111), .eq(comparator_6_eq));  // open: gt, lt
  Comparator #(.width(5)) comparator_7 (.a(opcode), .b(5'b01000), .eq(comparator_7_eq));  // open: gt, lt
  Comparator #(.width(5)) comparator_8 (.a(opcode), .b(5'b01001), .eq(comparator_8_eq));  // open: gt, lt
  Comparator #(.width(5)) comparator_9 (.a(opcode), .b(5'b01010), .eq(comparator_9_eq));  // open: gt, lt
  Comparator #(.width(5)) comparator_10 (.a(opcode), .b(5'b01011), .eq(comparator_10_eq));  // open: gt, lt
  Comparator #(.width(5)) comparator_11 (.a(opcode), .b(5'b01100), .eq(comparator_11_eq));  // open: gt, lt
  Comparator #(.width(5)) comparator_12 (.a(opcode), .b(5'b01101), .eq(comparator_12_eq));  // open: gt, lt
  Comparator #(.width(5)) comparator_13 (.a(opcode), .b({5{1'b0}}), .eq(comparator_13_eq));  // open: gt, lt
  Comparator #(.width(5)) comparator_14 (.a(opcode), .b(5'b00001), .eq(comparator_14_eq));  // open: gt, lt
  or or_1 (i_type, comparator_1_eq, comparator_2_eq, comparator_3_eq, comparator_4_eq, comparator_5_eq, comparator_6_eq, comparator_7_eq, comparator_8_eq, comparator_9_eq, comparator_10_eq, comparator_11_eq, comparator_12_eq);
  or or_2 (r_type, comparator_13_eq, comparator_14_eq);
endmodule
